// Logisim project 01_GATES_V.circ as structural Verilog: 19 circuits, main circuit main
module main (
  input  A,
  input  A_2,
  input  B,
  input  B_2,
  input  N_Type,
  input  in_6,
  input  in_7,
  input  [3:0] A_3,
  input  A_4,
  input  A_5,
  input  [3:0] B_3,
  input  B_4,
  input  B_5,
  input  C,
  input  C_2,
  input  D,
  input  [3:0] A_6,
  input  [3:0] B_6,
  input  in_19,
  input  in_20,
  input  in_21,
  input  in_22,
  output out_23,
  output out_24,
  output out_25,
  output out_26,
  output out_27,
  output out_28,
  output out_29,
  output out_30,
  output out_31,
  output out_32,
  output out_33,
  output out_34,
  output out_35,
  output out_36,
  output out_37,
  output out_38,
  output out_39,
  output out_40,
  output out_41,
  output out_42,
  output out_43,
  output out_44,
  output out_45,
  output out_46,
  output P_Type,
  output out_48,
  output out_49,
  output out_50,
  output out_51,
  output out_52,
  output out_53,
  output [3:0] out_54,
  output [3:0] out_55,
  output out_56,
  output out_57,
  output out_58,
  output out_59,
  output out_60,
  output out_61,
  output out_62,
  output out_63,
  output out_64,
  output out_65,
  output [3:0] out_66,
  output [3:0] out_67,
  output out_68,
  output out_69,
  output out_70,
  output out_71,
  output out_72,
  output [3:0] out_73,
  output [3:0] out_74,
  output out_75,
  output out_76,
  output out_77,
  output out_78,
  output out_79,
  output [3:0] out_80,
  output [3:0] out_81,
  output [3:0] out_82,
  output [3:0] out_83,
  output out_84,
  output out_85,
  output [3:0] out_86,
  output [3:0] out_87
);

  wire and_1_out, and_3_out, and_4_out, and_5_out, and_7_out, and_8_out, and_10_out, and_12_out, and_13_out,
       and_14_out, and_15_out, and_16_out, nand_5_out, nand_7_out, nand_8_out, nor_5_out, nor_6_out,
       nor_8_out, not_1_out, not_2_out, not_4_out, not_5_out, or_1_out, or_3_out, or_8_out, or_10_out,
       or_11_out, or_12_out, or_15_out, or_16_out;

  Transistor #(.\type ("n")) transistor_1 (.in(1'b1), .out(out_31), .gate(N_Type));
  Pull_Resistor pull_resistor_1 (.node(out_31));
  Transistor transistor_2 (.in(1'b1), .out(P_Type), .gate(N_Type));
  Pull_Resistor pull_resistor_2 (.node(P_Type));
  and and_1 (and_1_out, A_5, B_5);
  and and_2 (out_56, and_1_out, C_2);
  or or_1 (or_1_out, A_5, B_5);
  or or_2 (out_61, or_1_out, C_2);
  and and_3 (and_3_out, A_5, B_5);
  nand nand_1 (out_68, and_3_out, C_2);
  or or_3 (or_3_out, A_5, B_5);
  nor nor_1 (out_75, or_3_out, C_2);
  and and_4 (and_4_out, in_19, not_1_out);
  not not_1 (not_1_out, in_21);
  not not_2 (not_2_out, in_19);
  and and_5 (and_5_out, not_2_out, in_21);
  or or_4 (out_84, and_4_out, and_5_out);
  not not_3 (out_32, in_6);
  nand nand_2 (out_37, in_6, in_7);
  nor nor_2 (out_43, in_6, in_7);
  and and_6 (out_57, A_5, B_5, C_2);
  or or_5 (out_62, A_5, B_5, C_2);
  nand nand_3 (out_69, A_5, B_5, C_2);
  nor nor_3 (out_76, A_5, B_5, C_2);
  not not_4 (not_4_out, in_20);
  not not_5 (not_5_out, in_22);
  and and_7 (and_7_out, not_4_out, not_5_out);
  and and_8 (and_8_out, in_20, in_22);
  or or_6 (out_85, and_7_out, and_8_out);
  and and_9 (out_27, A_2, B_2);
  or or_7 (out_33, A_2, B_2);
  xor xor_1 (out_38, A_2, B_2);
  xnor xnor_1 (out_48, A_2, B_2);
  and and_10 (and_10_out, A_4, B_4);
  and and_11 (out_58, and_10_out, and_12_out);
  and and_12 (and_12_out, C, D);
  or or_8 (or_8_out, A_4, B_4);
  or or_9 (out_63, or_8_out, or_10_out);
  or or_10 (or_10_out, C, D);
  and and_13 (and_13_out, A_4, B_4);
  nand nand_4 (out_70, and_13_out, and_14_out);
  and and_14 (and_14_out, C, D);
  or or_11 (or_11_out, A_4, B_4);
  nor nor_4 (out_77, or_11_out, or_12_out);
  or or_12 (or_12_out, C, D);
  nand nand_5 (nand_5_out, A_2, B_2);
  nor nor_5 (nor_5_out, A_2, B_2);
  not not_6 (out_28, nand_5_out);
  not not_7 (out_34, nor_5_out);
  nor nor_6 (nor_6_out, A_2, B_2);
  nor nor_7 (out_39, nor_6_out, and_15_out);
  and and_15 (and_15_out, A_2, B_2);
  nor nor_8 (nor_8_out, A_2, B_2);
  or or_13 (out_49, nor_8_out, and_16_out);
  and and_16 (and_16_out, A_2, B_2);
  and and_17 (out_59, A_4, B_4, C, D);
  or or_14 (out_64, A_4, B_4, C, D);
  nand nand_6 (out_71, A_4, B_4, C, D);
  nor nor_9 (out_78, A_4, B_4, C, D);
  ET_4 et_4_1 (.in_1(A_4), .in_2(B_4), .in_3(C), .in_4(D), .out_5(out_60));
  OU_4 ou_4_1 (.in_1(A_4), .in_2(B_4), .in_3(C), .in_4(D), .out_5(out_65));
  NON_ET_4 non_et_4_1 (.in_1(A_4), .in_2(B_4), .in_3(C), .in_4(D), .out_5(out_72));
  NON_OU_4 non_ou_4_1 (.in_1(A_4), .in_2(B_4), .in_3(C), .in_4(D), .out_5(out_79));
  or or_15 (or_15_out, A_2, B_2);
  nand nand_7 (nand_7_out, A_2, B_2);
  or or_16 (or_16_out, A_2, B_2);
  nand nand_8 (nand_8_out, A_2, B_2);
  and and_18 (out_40, or_15_out, nand_7_out);
  nand nand_9 (out_50, or_16_out, nand_8_out);
  assign out_54 = A_3 & B_3;  // AND_Gate and_19, 4 bits wide
  assign out_66 = ~A_6;  // NOT_Gate not_8, 4 bits wide
  assign out_73 = ~(A_6 & B_6);  // NAND_Gate nand_10, 4 bits wide
  assign out_80 = ~(A_6 | B_6);  // NOR_Gate nor_10, 4 bits wide
  assign out_82 = A_6 & B_6;  // AND_Gate and_20, 4 bits wide
  assign out_86 = A_6 | B_6;  // OR_Gate or_17, 4 bits wide
  not not_9 (out_23, A);
  nand nand_11 (out_25, A, B);
  nor nor_11 (out_29, A, B);
  and and_21 (out_35, A, B);
  or or_18 (out_41, A, B);
  xnor xnor_2 (out_44, A, B);
  xor xor_2 (out_51, A, B);
  and and_22 (out_55[0], A_3[0], B_3[0]);
  and and_23 (out_55[1], A_3[1], B_3[1]);
  and and_24 (out_55[2], A_3[2], B_3[2]);
  and and_25 (out_55[3], A_3[3], B_3[3]);
  NON non_1 (.in_1(A), .out_2(out_24));
  NON_ET non_et_1 (.in_1(A), .in_2(B), .out_3(out_26));
  NON_OU non_ou_1 (.in_1(A), .in_2(B), .out_3(out_30));
  ET et_1 (.in_1(A), .in_2(B), .out_3(out_36));
  OU ou_1 (.in_1(A), .in_2(B), .out_3(out_42));
  NON_OU_EX non_ou_ex_1 (.in_1(A), .in_2(B), .out_3(out_45));
  OU_EX ou_ex_1 (.in_1(A), .in_2(B), .out_3(out_52));
  NON_4B non_4b_1 (.in_1(A_6), .out_2(out_67));
  NON_ET_4B non_et_4b_1 (.in_1(A_6), .in_2(B_6), .out_3(out_74));
  NON_OU_4B non_ou_4b_1 (.in_1(A_6), .in_2(B_6), .out_3(out_81));
  ET_4B et_4b_1 (.in_1(A_6), .in_2(B_6), .out_3(out_83));
  OU_4B ou_4b_1 (.in_1(A_6), .in_2(B_6), .out_3(out_87));
  NON_OU_EX_V2 non_ou_ex_v2_1 (.in_1(A), .in_2(B), .out_3(out_46));
  OU_EX_V2 ou_ex_v2_1 (.in_1(A), .in_2(B), .out_3(out_53));
endmodule

module NON (
  input  in_1,
  output out_2
);

  wire transistor_2_out;

  Transistor transistor_1 (.in(1'b1), .out(out_2), .gate(in_1));
  Pull_Resistor pull_resistor_1 (.node(out_2));
  Transistor #(.\type ("n")) transistor_2 (.in(out_2), .out(transistor_2_out), .gate(in_1));
  // also tied to GND on the sheet: transistor_2_out

  // Notes on the sheet:
  //   NON
  //   2 Transistors
endmodule

module NON_ET (
  input  in_1,
  input  in_2,
  output out_3
);

  wire transistor_2_out, transistor_3_out;

  Transistor transistor_1 (.in(1'b1), .out(out_3), .gate(in_1));
  Transistor #(.\type ("n")) transistor_2 (.in(out_3), .out(transistor_2_out), .gate(in_1));
  Transistor #(.\type ("n"), .gate("br")) transistor_3 (.in(transistor_2_out), .out(transistor_3_out), .gate(in_2));
  Transistor #(.gate("br")) transistor_4 (.in(1'b1), .out(out_3), .gate(in_2));
  Pull_Resistor pull_resistor_1 (.node(transistor_2_out));
  Pull_Resistor pull_resistor_2 (.node(out_3));
  // also tied to GND on the sheet: transistor_3_out

  // Notes on the sheet:
  //   NON-ET
  //   4 Transistors
endmodule

module NON_OU (
  input  in_1,
  input  in_2,
  output out_3
);

  wire transistor_1_out, transistor_3_out;

  Transistor #(.gate("br")) transistor_1 (.in(1'b1), .out(transistor_1_out), .gate(in_1));
  Transistor transistor_2 (.in(transistor_1_out), .out(out_3), .gate(in_2));
  Transistor #(.\type ("n"), .gate("br")) transistor_3 (.in(out_3), .out(transistor_3_out), .gate(in_1));
  Transistor #(.\type ("n")) transistor_4 (.in(out_3), .out(transistor_3_out), .gate(in_2));
  Pull_Resistor pull_resistor_1 (.node(transistor_1_out));
  Pull_Resistor pull_resistor_2 (.node(out_3));
  // also tied to GND on the sheet: transistor_3_out

  // Notes on the sheet:
  //   NON-OU
  //   4 Transistors
endmodule

module ET (
  input  in_1,
  input  in_2,
  output out_3
);

  wire transistor_1_out, transistor_2_out, transistor_3_out;

  Transistor transistor_1 (.in(1'b1), .out(transistor_1_out), .gate(in_1));
  Transistor #(.\type ("n")) transistor_2 (.in(transistor_1_out), .out(transistor_2_out), .gate(in_1));
  Transistor #(.\type ("n"), .gate("br")) transistor_3 (.in(transistor_2_out), .out(transistor_3_out), .gate(in_2));
  Transistor #(.gate("br")) transistor_4 (.in(1'b1), .out(transistor_1_out), .gate(in_2));
  Pull_Resistor pull_resistor_1 (.node(transistor_1_out));
  Pull_Resistor pull_resistor_2 (.node(transistor_2_out));
  Transistor transistor_5 (.in(1'b1), .out(out_3), .gate(transistor_1_out));
  Transistor #(.\type ("n")) transistor_6 (.in(out_3), .out(transistor_3_out), .gate(transistor_1_out));
  Pull_Resistor pull_resistor_3 (.node(out_3));
  // also tied to GND on the sheet: transistor_3_out

  // Notes on the sheet:
  //   NON-ET
  //   NON
  //   ET
  //   6 Transistors
endmodule

module OU (
  input  in_1,
  input  in_2,
  output out_3
);

  wire transistor_1_out, transistor_2_out, transistor_3_out;

  Transistor #(.gate("br")) transistor_1 (.in(1'b1), .out(transistor_1_out), .gate(in_1));
  Transistor transistor_2 (.in(transistor_1_out), .out(transistor_2_out), .gate(in_2));
  Transistor #(.\type ("n")) transistor_3 (.in(transistor_2_out), .out(transistor_3_out), .gate(in_2));
  Transistor #(.\type ("n"), .gate("br")) transistor_4 (.in(transistor_2_out), .out(transistor_3_out), .gate(in_1));
  Pull_Resistor pull_resistor_1 (.node(transistor_2_out));
  Pull_Resistor pull_resistor_2 (.node(transistor_1_out));
  Transistor transistor_5 (.in(1'b1), .out(out_3), .gate(transistor_2_out));
  Pull_Resistor pull_resistor_3 (.node(out_3));
  Transistor #(.\type ("n")) transistor_6 (.in(out_3), .out(transistor_3_out), .gate(transistor_2_out));
  // also tied to GND on the sheet: transistor_3_out

  // Notes on the sheet:
  //   NON-OU
  //   NON
  //   OU
  //   6 Transistors
endmodule

module NON_OU_EX (
  input  in_1,
  input  in_2,
  output out_3
);

  wire transistor_1_out, transistor_2_out, transistor_3_out, transistor_5_out, transistor_6_out,
       transistor_7_out, transistor_9_out, transistor_11_out, transistor_12_out, transistor_13_out;

  Transistor transistor_1 (.in(1'b1), .out(transistor_1_out), .gate(in_1));
  Transistor #(.\type ("n")) transistor_2 (.in(transistor_1_out), .out(transistor_2_out), .gate(in_1));
  Transistor #(.\type ("n"), .gate("br")) transistor_3 (.in(transistor_2_out), .out(transistor_3_out), .gate(in_2));
  Transistor #(.gate("br")) transistor_4 (.in(1'b1), .out(transistor_1_out), .gate(in_2));
  Pull_Resistor pull_resistor_1 (.node(transistor_2_out));
  Transistor #(.gate("br")) transistor_5 (.in(1'b1), .out(transistor_5_out), .gate(in_2));
  Transistor transistor_6 (.in(transistor_5_out), .out(transistor_6_out), .gate(in_1));
  Transistor #(.\type ("n")) transistor_7 (.in(transistor_6_out), .out(transistor_7_out), .gate(in_1));
  Transistor #(.\type ("n"), .gate("br")) transistor_8 (.in(transistor_6_out), .out(transistor_7_out), .gate(in_2));
  Pull_Resistor pull_resistor_2 (.node(transistor_1_out));
  Pull_Resistor pull_resistor_3 (.node(transistor_5_out));
  Pull_Resistor pull_resistor_4 (.node(transistor_6_out));
  Transistor transistor_9 (.in(1'b1), .out(transistor_9_out), .gate(transistor_1_out));
  Pull_Resistor pull_resistor_5 (.node(transistor_9_out));
  Transistor #(.\type ("n")) transistor_10 (.in(transistor_9_out), .out(transistor_3_out), .gate(transistor_1_out));
  Transistor #(.gate("br")) transistor_11 (.in(1'b1), .out(transistor_11_out), .gate(transistor_9_out));
  Transistor transistor_12 (.in(transistor_11_out), .out(transistor_12_out), .gate(transistor_6_out));
  Transistor #(.\type ("n"), .gate("br")) transistor_13 (
    .in(transistor_12_out), .out(transistor_13_out), .gate(transistor_9_out));
  Transistor #(.\type ("n")) transistor_14 (.in(transistor_12_out), .out(transistor_13_out), .gate(transistor_6_out));
  Pull_Resistor pull_resistor_6 (.node(transistor_12_out));
  Pull_Resistor pull_resistor_7 (.node(transistor_11_out));
  Transistor transistor_15 (.in(1'b1), .out(out_3), .gate(transistor_12_out));
  Transistor #(.\type ("n")) transistor_16 (.in(out_3), .out(transistor_13_out), .gate(transistor_12_out));
  Pull_Resistor pull_resistor_8 (.node(out_3));
  // also tied to GND on the sheet: {transistor_7_out, transistor_3_out, transistor_13_out}

  // Notes on the sheet:
  //   NON-ET
  //   NON
  //   NON-OU
  //   ET
  //   NON-OU
  //   NON
  //   OU
  //   16 Transistors
endmodule

module OU_EX (
  input  in_1,
  input  in_2,
  output out_3
);

  wire transistor_1_out, transistor_2_out, transistor_3_out, transistor_4_out, transistor_5_out,
       transistor_6_out, transistor_9_out, transistor_11_out, transistor_13_out;

  Transistor transistor_1 (.in(1'b1), .out(transistor_1_out), .gate(in_1));
  Transistor #(.\type ("n")) transistor_2 (.in(transistor_1_out), .out(transistor_2_out), .gate(in_1));
  Transistor #(.\type ("n"), .gate("br")) transistor_3 (.in(transistor_2_out), .out(transistor_3_out), .gate(in_2));
  Transistor #(.gate("br")) transistor_4 (.in(1'b1), .out(transistor_4_out), .gate(in_1));
  Transistor transistor_5 (.in(transistor_4_out), .out(transistor_5_out), .gate(in_2));
  Transistor #(.\type ("n"), .gate("br")) transistor_6 (.in(transistor_5_out), .out(transistor_6_out), .gate(in_1));
  Transistor #(.\type ("n")) transistor_7 (.in(transistor_5_out), .out(transistor_6_out), .gate(in_2));
  Transistor #(.gate("br")) transistor_8 (.in(1'b1), .out(transistor_1_out), .gate(in_2));
  Pull_Resistor pull_resistor_1 (.node(transistor_1_out));
  Pull_Resistor pull_resistor_2 (.node(transistor_2_out));
  Pull_Resistor pull_resistor_3 (.node(transistor_5_out));
  Pull_Resistor pull_resistor_4 (.node(transistor_4_out));
  Transistor transistor_9 (.in(1'b1), .out(transistor_9_out), .gate(transistor_1_out));
  Transistor #(.\type ("n")) transistor_10 (.in(transistor_9_out), .out(transistor_3_out), .gate(transistor_1_out));
  Pull_Resistor pull_resistor_5 (.node(transistor_9_out));
  Transistor #(.gate("br")) transistor_11 (.in(1'b1), .out(transistor_11_out), .gate(transistor_5_out));
  Transistor transistor_12 (.in(transistor_11_out), .out(out_3), .gate(transistor_9_out));
  Transistor #(.\type ("n"), .gate("br")) transistor_13 (.in(out_3), .out(transistor_13_out), .gate(transistor_5_out));
  Transistor #(.\type ("n")) transistor_14 (.in(out_3), .out(transistor_13_out), .gate(transistor_9_out));
  Pull_Resistor pull_resistor_6 (.node(out_3));
  Pull_Resistor pull_resistor_7 (.node(transistor_11_out));
  // also tied to GND on the sheet: {transistor_3_out, transistor_6_out, transistor_13_out}

  // Notes on the sheet:
  //   NON-ET
  //   NON-OU
  //   NON
  //   ET
  //   NON-OU
  //   OU_EX
  //   14 Transistors
endmodule

module NON_OU_EX_V2 (
  input  in_1,
  input  in_2,
  output out_3
);

  wire transistor_1_out, transistor_2_out, transistor_3_out, transistor_5_out, transistor_6_out,
       transistor_7_out, transistor_8_out, transistor_12_out, transistor_13_out;

  Transistor #(.gate("br")) transistor_1 (.in(1'b1), .out(transistor_1_out), .gate(in_1));
  Transistor transistor_2 (.in(transistor_1_out), .out(transistor_2_out), .gate(in_2));
  Transistor #(.\type ("n"), .gate("br")) transistor_3 (.in(transistor_2_out), .out(transistor_3_out), .gate(in_1));
  Transistor #(.\type ("n")) transistor_4 (.in(transistor_2_out), .out(transistor_3_out), .gate(in_2));
  Pull_Resistor pull_resistor_1 (.node(transistor_2_out));
  Pull_Resistor pull_resistor_2 (.node(transistor_1_out));
  Transistor transistor_5 (.in(1'b1), .out(transistor_5_out), .gate(in_2));
  Transistor #(.\type ("n")) transistor_6 (.in(transistor_5_out), .out(transistor_6_out), .gate(in_2));
  Transistor #(.\type ("n"), .gate("br")) transistor_7 (.in(transistor_6_out), .out(transistor_7_out), .gate(in_1));
  Transistor transistor_8 (.in(1'b1), .out(transistor_8_out), .gate(transistor_2_out));
  Transistor #(.\type ("n")) transistor_9 (.in(transistor_8_out), .out(transistor_3_out), .gate(transistor_2_out));
  Transistor #(.gate("br")) transistor_10 (.in(1'b1), .out(transistor_5_out), .gate(in_1));
  Pull_Resistor pull_resistor_3 (.node(transistor_6_out));
  Pull_Resistor pull_resistor_4 (.node(transistor_5_out));
  Pull_Resistor pull_resistor_5 (.node(transistor_8_out));
  Transistor transistor_11 (.in(1'b1), .out(out_3), .gate(transistor_8_out));
  Transistor #(.\type ("n")) transistor_12 (.in(out_3), .out(transistor_12_out), .gate(transistor_8_out));
  Transistor #(.\type ("n"), .gate("br")) transistor_13 (
    .in(transistor_12_out), .out(transistor_13_out), .gate(transistor_5_out));
  Transistor #(.gate("br")) transistor_14 (.in(1'b1), .out(out_3), .gate(transistor_5_out));
  Pull_Resistor pull_resistor_6 (.node(out_3));
  Pull_Resistor pull_resistor_7 (.node(transistor_12_out));
  // also tied to GND on the sheet: {transistor_3_out, transistor_7_out, transistor_13_out}

  // Notes on the sheet:
  //   NON-OU
  //   NON-ET
  //   NON
  //   OU
  //   NON-ET
  //   14 Transistors
endmodule

module OU_EX_V2 (
  input  in_1,
  input  in_2,
  output out_3
);

  wire transistor_1_out, transistor_2_out, transistor_3_out, transistor_5_out, transistor_6_out,
       transistor_7_out, transistor_8_out, transistor_11_out, transistor_12_out, transistor_13_out;

  Transistor #(.gate("br")) transistor_1 (.in(1'b1), .out(transistor_1_out), .gate(in_1));
  Transistor transistor_2 (.in(transistor_1_out), .out(transistor_2_out), .gate(in_2));
  Transistor #(.\type ("n"), .gate("br")) transistor_3 (.in(transistor_2_out), .out(transistor_3_out), .gate(in_1));
  Transistor #(.\type ("n")) transistor_4 (.in(transistor_2_out), .out(transistor_3_out), .gate(in_2));
  Pull_Resistor pull_resistor_1 (.node(transistor_1_out));
  Pull_Resistor pull_resistor_2 (.node(transistor_2_out));
  Transistor transistor_5 (.in(1'b1), .out(transistor_5_out), .gate(in_2));
  Transistor #(.\type ("n")) transistor_6 (.in(transistor_5_out), .out(transistor_6_out), .gate(in_2));
  Transistor #(.\type ("n"), .gate("br")) transistor_7 (.in(transistor_6_out), .out(transistor_7_out), .gate(in_1));
  Transistor transistor_8 (.in(1'b1), .out(transistor_8_out), .gate(transistor_2_out));
  Transistor #(.\type ("n")) transistor_9 (.in(transistor_8_out), .out(transistor_3_out), .gate(transistor_2_out));
  Transistor #(.gate("br")) transistor_10 (.in(1'b1), .out(transistor_5_out), .gate(in_1));
  Pull_Resistor pull_resistor_3 (.node(transistor_6_out));
  Pull_Resistor pull_resistor_4 (.node(transistor_5_out));
  Pull_Resistor pull_resistor_5 (.node(transistor_8_out));
  Transistor transistor_11 (.in(1'b1), .out(transistor_11_out), .gate(transistor_8_out));
  Transistor #(.\type ("n")) transistor_12 (.in(transistor_11_out), .out(transistor_12_out), .gate(transistor_8_out));
  Transistor #(.\type ("n"), .gate("br")) transistor_13 (
    .in(transistor_12_out), .out(transistor_13_out), .gate(transistor_5_out));
  Transistor #(.gate("br")) transistor_14 (.in(1'b1), .out(transistor_11_out), .gate(transistor_5_out));
  Pull_Resistor pull_resistor_6 (.node(transistor_12_out));
  Pull_Resistor pull_resistor_7 (.node(transistor_11_out));
  Transistor transistor_15 (.in(1'b1), .out(out_3), .gate(transistor_11_out));
  Pull_Resistor pull_resistor_8 (.node(out_3));
  Transistor #(.\type ("n")) transistor_16 (.in(out_3), .out(transistor_13_out), .gate(transistor_11_out));
  // also tied to GND on the sheet: {transistor_3_out, transistor_7_out, transistor_13_out}

  // Notes on the sheet:
  //   NON-OU
  //   NON-ET
  //   NON
  //   OU
  //   NON-ET
  //   NON
  //   ET
  //   16 Transistors
endmodule

module NON_ET_4 (
  input  in_1,
  input  in_2,
  input  in_3,
  input  in_4,
  output out_5
);

  wire et_1_out_3, et_2_out_3;

  ET et_1 (.in_1(in_1), .in_2(in_2), .out_3(et_1_out_3));
  ET et_2 (.in_1(in_3), .in_2(in_4), .out_3(et_2_out_3));
  NON_ET non_et_1 (.in_1(et_1_out_3), .in_2(et_2_out_3), .out_3(out_5));
endmodule

module NON_OU_4 (
  input  in_1,
  input  in_2,
  input  in_3,
  input  in_4,
  output out_5
);

  wire ou_1_out_3, ou_2_out_3;

  OU ou_1 (.in_1(in_1), .in_2(in_2), .out_3(ou_1_out_3));
  OU ou_2 (.in_1(in_3), .in_2(in_4), .out_3(ou_2_out_3));
  NON_OU non_ou_1 (.in_1(ou_1_out_3), .in_2(ou_2_out_3), .out_3(out_5));
endmodule

module ET_4 (
  input  in_1,
  input  in_2,
  input  in_3,
  input  in_4,
  output out_5
);

  wire et_1_out_3, et_2_out_3;

  ET et_1 (.in_1(in_1), .in_2(in_2), .out_3(et_1_out_3));
  ET et_2 (.in_1(in_3), .in_2(in_4), .out_3(et_2_out_3));
  ET et_3 (.in_1(et_1_out_3), .in_2(et_2_out_3), .out_3(out_5));
endmodule

module OU_4 (
  input  in_1,
  input  in_2,
  input  in_3,
  input  in_4,
  output out_5
);

  wire ou_1_out_3, ou_2_out_3;

  OU ou_1 (.in_1(in_1), .in_2(in_2), .out_3(ou_1_out_3));
  OU ou_2 (.in_1(in_3), .in_2(in_4), .out_3(ou_2_out_3));
  OU ou_3 (.in_1(ou_1_out_3), .in_2(ou_2_out_3), .out_3(out_5));
endmodule

module NON_4B (
  input  [3:0] in_1,
  output [3:0] out_2
);

  NON non_1 (.in_1(in_1[0]), .out_2(out_2[0]));
  NON non_2 (.in_1(in_1[1]), .out_2(out_2[1]));
  NON non_3 (.in_1(in_1[2]), .out_2(out_2[2]));
  NON non_4 (.in_1(in_1[3]), .out_2(out_2[3]));
endmodule

module NON_ET_4B (
  input  [3:0] in_1,
  input  [3:0] in_2,
  output [3:0] out_3
);

  NON_ET non_et_1 (.in_1(in_1[0]), .in_2(in_2[0]), .out_3(out_3[0]));
  NON_ET non_et_2 (.in_1(in_1[1]), .in_2(in_2[1]), .out_3(out_3[1]));
  NON_ET non_et_3 (.in_1(in_1[2]), .in_2(in_2[2]), .out_3(out_3[2]));
  NON_ET non_et_4 (.in_1(in_1[3]), .in_2(in_2[3]), .out_3(out_3[3]));
endmodule

module NON_OU_4B (
  input  [3:0] in_1,
  input  [3:0] in_2,
  output [3:0] out_3
);

  NON_OU non_ou_1 (.in_1(in_1[0]), .in_2(in_2[0]), .out_3(out_3[0]));
  NON_OU non_ou_2 (.in_1(in_1[1]), .in_2(in_2[1]), .out_3(out_3[1]));
  NON_OU non_ou_3 (.in_1(in_1[2]), .in_2(in_2[2]), .out_3(out_3[2]));
  NON_OU non_ou_4 (.in_1(in_1[3]), .in_2(in_2[3]), .out_3(out_3[3]));
endmodule

module ET_4B (
  input  [3:0] in_1,
  input  [3:0] in_2,
  output [3:0] out_3
);

  ET et_1 (.in_1(in_1[0]), .in_2(in_2[0]), .out_3(out_3[0]));
  ET et_2 (.in_1(in_1[1]), .in_2(in_2[1]), .out_3(out_3[1]));
  ET et_3 (.in_1(in_1[2]), .in_2(in_2[2]), .out_3(out_3[2]));
  ET et_4 (.in_1(in_1[3]), .in_2(in_2[3]), .out_3(out_3[3]));
endmodule

module OU_4B (
  input  [3:0] in_1,
  input  [3:0] in_2,
  output [3:0] out_3
);

  OU ou_1 (.in_1(in_1[0]), .in_2(in_2[0]), .out_3(out_3[0]));
  OU ou_2 (.in_1(in_1[1]), .in_2(in_2[1]), .out_3(out_3[1]));
  OU ou_3 (.in_1(in_1[2]), .in_2(in_2[2]), .out_3(out_3[2]));
  OU ou_4 (.in_1(in_1[3]), .in_2(in_2[3]), .out_3(out_3[3]));
endmodule
