// Logisim project 02_PLEXERS_V.circ as structural Verilog: 19 circuits, main circuit main
module main (
  input  [1:0] A,
  input  [2:0] in_2,
  input  in_3,
  input  ENABLE,
  input  [3:0] in_5,
  input  [1:0] in_6,
  input  [7:0] in_7,
  input  Input,
  input  in_9,
  input  in_10,
  input  in_11,
  input  [1:0] in_12,
  input  in_13,
  input  [1:0] in_14,
  input  [1:0] Other_jar,
  input  [1:0] Input_2,
  input  [1:0] in_17,
  input  [1:0] in_18,
  input  [3:0] in_19,
  input  in_20,
  input  [7:0] in_21,
  input  in_22,
  input  [15:0] in_23,
  input  in_24,
  input  in_25,
  input  in_26,
  input  in_27,
  input  [3:0] in_28,
  output [3:0] out_29,
  output [3:0] out_30,
  output [3:0] out_31,
  output [3:0] out_32,
  output [3:0] out_33,
  output [3:0] out_34,
  output [3:0] out_35,
  output out_36,
  output [2:0] Other_jar_2,
  output out_38,
  output out_39,
  output [1:0] out_40,
  output [2:0] out_41,
  output [3:0] out_42,
  output [3:0] out_43,
  output out_44,
  output out_45,
  output out_46,
  output out_47,
  output [2:0] out_48,
  output [1:0] out_49,
  output [1:0] out_50,
  output [1:0] out_51,
  output [1:0] out_52,
  output [1:0] out_53,
  output [1:0] out_54,
  output [1:0] out_55,
  output [1:0] out_56,
  output [1:0] out_57,
  output [1:0] out_58,
  output out_59,
  output out_60,
  output out_61,
  output [1:0] out_62,
  output [1:0] out_63,
  output [2:0] out_64,
  output out_65,
  output out_66,
  output out_67,
  output out_68,
  output out_69,
  output [2:0] out_70,
  output [2:0] out_71,
  output [2:0] out_72,
  output [3:0] out_73,
  output [3:0] out_74,
  output [15:0] out_75,
  output [15:0] out_76,
  output [1:0] out_77,
  output [1:0] out_78,
  output [1:0] out_79,
  output [1:0] out_80
);

  wire decoder_5_out0, decoder_5_out1, decoder_5_out2, decoder_5_out3, decoder_6_out0, decoder_6_out1,
       decoder_6_out2, decoder_6_out3, decoder_6_out4, decoder_6_out5, decoder_6_out6, decoder_6_out7,
       demultiplexer_3_out0, demultiplexer_3_out1, demultiplexer_3_out2, demultiplexer_3_out3;

  DEC0 dec0_1 (.SEL(A), .Output_0(out_29[0]), .Output_1(out_29[1]), .Output_2(out_29[2]), .Output_3(out_29[3]));
  DMX1 dmx1_1 (
    .Sel(A), .Input(Input), .ENABLE(ENABLE), .Output_0(out_42[0]), .Output_1(out_42[1]),
    .Output_2(out_42[2]), .Ouput_3(out_42[3]));
  DMX2 dmx2_1 (
    .Sel(A), .Input(Input_2), .ENABLE(ENABLE), .Output_0(out_49), .Output_1(out_51), .Output_2(out_53),
    .Output_3(out_57));
  // Coder coder_1: pin names not known; wires that end beside it: in_21[0], in_21[1], in_21[2], in_21[3], in_21[4], in_21[5], in_21[6], in_21[7], out_65, in_22, out_71
  Decoder #(.disabled(0), .enable("false")) decoder_1 (.out0(out_77[0]), .out1(out_77[1]), .sel(in_25));
  Decoder #(.select(2), .enable("false")) decoder_2 (
    .out0(out_30[0]), .out1(out_30[1]), .out2(out_30[2]), .out3(out_30[3]), .sel(A));
  Demultiplexer #(.select(2), .disabled(0)) demultiplexer_1 (
    .out0(out_43[0]), .out1(out_43[1]), .out2(out_43[2]), .out3(out_43[3]), .in(Input), .sel(A), .en(ENABLE));
  Demultiplexer #(.select(2), .width(2), .disabled(0)) demultiplexer_2 (
    .out0(out_50), .out1(out_52), .out2(out_54), .out3(out_58), .in(Input_2), .sel(A), .en(ENABLE));
  // Probe on out_71
  // Probe on out_71
  COD8 cod8_1 (
    .Enable(in_22), .Validate(out_66), .Output(out_72), .Input_0(in_21[0]), .Input_1(in_21[1]),
    .Input_2(in_21[2]), .Input_3(in_21[3]), .Input_4(in_21[4]), .Input_5(in_21[5]), .Input_6(in_21[6]),
    .Input_7(in_21[7]));
  DED0 ded0_1 (.in_1(in_25), .Output_0(out_78[0]), .Output_1(out_78[1]));
  DET0 det0_1 (.SEL(A), .Output_0(out_31[0]), .Output_1(out_31[1]), .Output_2(out_31[2]), .Output_3(out_31[3]));
  // Probe on out_72
  // Probe on out_72
  DECE dece_1 (
    .SEL(A), .ENABLE(ENABLE), .Output_0(out_32[0]), .Output_1(out_32[1]), .Output_2(out_32[2]),
    .Output_3(out_32[3]));
  MUX1 mux1_1 (
    .Sel(A), .Input_0(in_5[0]), .Input_1(in_5[1]), .Input_2(in_5[2]), .Input_3(in_5[3]), .ENABLE(ENABLE),
    .Ouput(out_44));
  MUX2 mux2_1 (
    .Sel(A), .Input_0(in_12), .Input_1(in_14), .Input_2(in_17), .Input_3(in_18), .ENABLE(ENABLE),
    .Output(out_55));
  Decoder #(.disabled(0)) decoder_3 (.out0(out_79[0]), .out1(out_79[1]), .sel(in_25), .en(in_26));
  Multiplexer #(.select(2), .disabled(0)) multiplexer_1 (
    .in0(in_5[0]), .in1(in_5[1]), .in2(in_5[2]), .in3(in_5[3]), .out(out_45), .sel(A), .en(ENABLE));
  Multiplexer #(.select(2), .width(2), .disabled(0)) multiplexer_2 (
    .in0(in_12), .in1(in_14), .in2(in_17), .in3(in_18), .out(out_56), .sel(A), .en(ENABLE));
  DEDE dede_1 (.in_1(in_25), .in_2(in_26), .Output_0(out_80[0]), .Output_1(out_80[1]));
  Decoder #(.select(2), .disabled(0)) decoder_4 (
    .out0(out_33[0]), .out1(out_33[1]), .out2(out_33[2]), .out3(out_33[3]), .sel(A), .en(ENABLE));
  CODH codh_1 (
    .Enable(in_24), .Validate(out_67), .Output(out_73), .Input_0(in_23[0]), .Input_1(in_23[1]),
    .Input_2(in_23[2]), .Input_3(in_23[3]), .Input_4(in_23[4]), .Input_5(in_23[5]), .Input_6(in_23[6]),
    .Input_7(in_23[7]), .Input_8(in_23[8]), .Input_9(in_23[9]), .Input_10(in_23[10]), .Input_11(in_23[11]),
    .Input_12(in_23[12]), .Input_13(in_23[13]), .Input_14(in_23[14]), .Input_15(in_23[15]));
  // Probe on out_73
  // Probe on out_73
  DT0E dt0e_1 (
    .SEL(A), .ENABLE(ENABLE), .Output_0(out_34[0]), .Output_1(out_34[1]), .Output_2(out_34[2]),
    .Output_3(out_34[3]));
  Decoder #(.select(2), .disabled(0)) decoder_5 (
    .out0(decoder_5_out0), .out1(decoder_5_out1), .out2(decoder_5_out2), .out3(decoder_5_out3), .sel(in_6),
    .en(in_9));
  Demultiplexer #(.select(2), .disabled(0)) demultiplexer_3 (
    .out0(demultiplexer_3_out0), .out1(demultiplexer_3_out1), .out2(demultiplexer_3_out2),
    .out3(demultiplexer_3_out3), .in(in_11), .sel(Other_jar), .en(in_13));
  // Coder coder_2: pin names not known; wires that end beside it: in_19[0], in_19[1], in_19[2], in_19[3], out_59, in_20, out_62
  // Coder coder_3: pin names not known; wires that end beside it: decoder_5_out0, decoder_5_out1, decoder_5_out2, decoder_5_out3, out_39, in_9, out_40
  Multiplexer #(.select(2), .disabled(0)) multiplexer_3 (
    .in0(demultiplexer_3_out0), .in1(demultiplexer_3_out1), .in2(demultiplexer_3_out2),
    .in3(demultiplexer_3_out3), .out(out_47), .sel(Other_jar), .en(in_13));
  DT0E dt0e_2 (
    .SEL(A), .ENABLE(ENABLE), .Output_0(out_35[0]), .Output_1(out_35[1]), .Output_2(out_35[2]),
    .Output_3(out_35[3]));
  COD4 cod4_1 (
    .Enable(in_20), .Output(out_63), .Validate(out_60), .Input_0(in_19[0]), .Input_1(in_19[1]),
    .Input_2(in_19[2]), .Input_3(in_19[3]));
  // Coder coder_4: pin names not known; wires that end beside it: in_23[0], in_23[1], in_23[2], in_23[3], in_23[4], in_23[5], in_23[6], in_23[7], in_23[8], in_23[9], in_23[10], in_23[11], in_23[12], in_23[13], in_23[14], in_23[15], out_68, in_24, out_74
  // Probe on out_74
  // Probe on out_74
  Decoder #(.select(3), .disabled(0)) decoder_6 (
    .out0(decoder_6_out0), .out1(decoder_6_out1), .out2(decoder_6_out2), .out3(decoder_6_out3),
    .out4(decoder_6_out4), .out5(decoder_6_out5), .out6(decoder_6_out6), .out7(decoder_6_out7), .sel(in_2),
    .en(in_3));
  // Coder coder_5: pin names not known; wires that end beside it: decoder_6_out0, decoder_6_out1, decoder_6_out2, decoder_6_out3, decoder_6_out4, decoder_6_out5, decoder_6_out6, decoder_6_out7, out_36, in_3, Other_jar_2
  // Probe on out_41
  COD8 cod8_2 (
    .Enable(in_10), .Validate(out_38), .Output(out_41), .Input_0(in_7[0]), .Input_1(in_7[1]),
    .Input_2(in_7[2]), .Input_3(in_7[3]), .Input_4(in_7[4]), .Input_5(in_7[5]), .Input_6(in_7[6]),
    .Input_7(in_7[7]));
  // Probe on out_48
  COD8 cod8_3 (
    .Input_7(in_7[7]), .Input_6(in_7[6]), .Input_5(in_7[5]), .Input_4(in_7[4]), .Input_3(in_7[3]),
    .Input_2(in_7[2]), .Input_1(in_7[1]), .Input_0(in_7[0]), .Enable(in_10), .Validate(out_46),
    .Output(out_48));
  // Probe on out_64
  // Coder coder_6: pin names not known; wires that end beside it: in_7[0], in_7[1], in_7[2], in_7[3], in_7[4], in_7[5], in_7[6], in_7[7], out_61, in_10, out_64
  // Probe on out_70
  // Coder coder_7: pin names not known; wires that end beside it: in_7[0], in_7[1], in_7[2], in_7[3], in_7[4], in_7[5], in_7[6], in_7[7], out_69, in_10, out_70
  Decoder #(.select(4), .disabled(0)) decoder_7 (
    .out0(out_75[0]), .out1(out_75[1]), .out2(out_75[2]), .out3(out_75[3]), .out4(out_75[4]),
    .out5(out_75[5]), .out6(out_75[6]), .out7(out_75[7]), .out8(out_75[8]), .out9(out_75[9]),
    .out10(out_75[10]), .out11(out_75[11]), .out12(out_75[12]), .out13(out_75[13]), .out14(out_75[14]),
    .out15(out_75[15]), .sel(in_28), .en(in_27));
  DT4E dt4e_1 (
    .in_1(in_27), .in_2(in_28), .Output_00(out_76[0]), .Output_01(out_76[1]), .Output_02(out_76[2]),
    .Output_03(out_76[3]), .Output_04(out_76[4]), .Output_05(out_76[5]), .Output_06(out_76[6]),
    .Output_07(out_76[7]), .Output_08(out_76[8]), .Output_09(out_76[9]), .Output_10(out_76[10]),
    .Output_11(out_76[11]), .Output_12(out_76[12]), .Output_13(out_76[13]), .Output_14(out_76[14]),
    .Output_16(out_76[15]));

  // Notes on the sheet:
  //   Other.jar
  //   other_chip8_lib.circ
  //   other_chip8.circ
  //   Other.jar
  //   other_chip8_lib.circ
  //   Other.jar
  //   Other.jar
  //   Other.jar
  //   other_chip8_lib.circ
  //   other_chip8_lib.circ
endmodule

module main2 (
  input  [3:0] in_1,
  input  [3:0] in_2,
  input  in_3,
  input  [1:0] in_4,
  output out_5,
  output [1:0] out_6,
  output out_7,
  output out_8,
  output out_9,
  output [1:0] out_10,
  output out_11,
  output out_12,
  output [1:0] out_13,
  output out_14,
  output [1:0] out_15,
  output out_16,
  output out_17,
  output [1:0] out_18
);

  wire not_1_out;
  wire [1:0] bit_extender_1_out, priority_encoder_2_out;

  // Coder coder_1: pin names not known; wires that end beside it: in_1[0], in_1[1], in_1[2], in_1[3], out_5, in_3, out_6
  Priority_Encoder #(.select(2), .disabled(0)) priority_encoder_1 (
    .in0(in_1[0]), .in1(in_1[1]), .in2(in_1[2]), .in3(in_1[3]), .out(out_10), .gs(out_9), .en_out(out_8),
    .en_in(in_3));
  COD4 cod4_1 (
    .Input_0(in_1[0]), .Input_1(in_1[1]), .Input_2(in_1[2]), .Input_3(in_1[3]), .Enable(in_3),
    .Validate(out_12), .Output(out_13));
  // Coder coder_2: pin names not known; wires that end beside it: in_1[0], in_1[1], in_1[2], in_1[3], out_14, in_3, out_15
  Priority_Encoder #(.select(2), .disabled(0)) priority_encoder_2 (
    .in0(in_1[0]), .in1(in_1[1]), .in2(in_1[2]), .in3(in_1[3]), .out(priority_encoder_2_out), .gs(out_17),
    .en_out(out_16), .en_in(in_3));
  not not_1 (not_1_out, out_16);
  assign bit_extender_1_out = {{1{not_1_out}}, not_1_out};  // Bit_Extender bit_extender_1
  assign out_18 = priority_encoder_2_out & bit_extender_1_out;  // AND_Gate and_1, 2 bits wide
  Multiplexer #(.select(2), .enable("false")) multiplexer_1 (
    .in0(in_2[0]), .in1(in_2[1]), .in2(in_2[2]), .in3(in_2[3]), .out(out_7), .sel(in_4));
  BitSelector #(.width(4)) bitselector_1 (.in(in_2), .out(out_11), .sel(in_4));
endmodule

module main64 (
  input  in_1,
  input  [5:0] in_2,
  input  [5:0] in_3,
  input  [5:0] in_4,
  input  in_5,
  input  in_6,
  input  in_7,
  input  in_8,
  input  [31:0] in_9,
  input  [31:0] in_10,
  output out_11,
  output out_12,
  output out_13,
  output out_14,
  output out_15,
  output out_16,
  output out_17,
  output out_18,
  output out_19,
  output out_20,
  output out_21,
  output out_22,
  output out_23,
  output out_24,
  output out_25,
  output out_26,
  output out_27,
  output out_28,
  output out_29,
  output out_30,
  output out_31,
  output out_32,
  output out_33,
  output out_34,
  output out_35,
  output out_36,
  output out_37,
  output out_38,
  output out_39,
  output out_40,
  output out_41,
  output out_42,
  output out_43,
  output out_44,
  output out_45,
  output out_46,
  output out_47,
  output out_48,
  output out_49,
  output out_50,
  output out_51,
  output out_52,
  output out_53,
  output out_54,
  output out_55,
  output out_56,
  output out_57,
  output out_58,
  output out_59,
  output out_60,
  output out_61,
  output out_62,
  output out_63,
  output out_64,
  output out_65,
  output out_66,
  output out_67,
  output out_68,
  output out_69,
  output out_70,
  output out_71,
  output out_72,
  output out_73,
  output out_74,
  output out_75,
  output [31:0] out_76,
  output [31:0] out_77,
  output [31:0] out_78,
  output [31:0] out_79
);

  wire button_1_out, button_2_out, decoder_1_out0, decoder_1_out1, decoder_2_out0, decoder_2_out1,
       decoder_5_out0, decoder_5_out1, decoder_6_out0, decoder_6_out1, multiplexer_1_out, multiplexer_2_out;
  wire [5:0] counter_1_q;

  Demultiplexer #(.select(5), .disabled(0)) demultiplexer_1 (
    .out0(out_77[0]), .out1(out_77[1]), .out2(out_77[2]), .out3(out_77[3]), .out4(out_77[4]),
    .out5(out_77[5]), .out6(out_77[6]), .out7(out_77[7]), .out8(out_77[8]), .out9(out_77[9]),
    .out10(out_77[10]), .out11(out_77[11]), .out12(out_77[12]), .out13(out_77[13]), .out14(out_77[14]),
    .out15(out_77[15]), .out16(out_77[16]), .out17(out_77[17]), .out18(out_77[18]), .out19(out_77[19]),
    .out20(out_77[20]), .out21(out_77[21]), .out22(out_77[22]), .out23(out_77[23]), .out24(out_77[24]),
    .out25(out_77[25]), .out26(out_77[26]), .out27(out_77[27]), .out28(out_77[28]), .out29(out_77[29]),
    .out30(out_77[30]), .out31(out_77[31]), .in(in_1), .sel(in_2[4:0]), .en(decoder_1_out0));
  Decoder #(.disabled(0)) decoder_1 (.out0(decoder_1_out0), .out1(decoder_1_out1), .sel(in_2[5]), .en(in_7));
  Demultiplexer #(.select(5), .disabled(0)) demultiplexer_2 (
    .out0(out_76[0]), .out1(out_76[1]), .out2(out_76[2]), .out3(out_76[3]), .out4(out_76[4]),
    .out5(out_76[5]), .out6(out_76[6]), .out7(out_76[7]), .out8(out_76[8]), .out9(out_76[9]),
    .out10(out_76[10]), .out11(out_76[11]), .out12(out_76[12]), .out13(out_76[13]), .out14(out_76[14]),
    .out15(out_76[15]), .out16(out_76[16]), .out17(out_76[17]), .out18(out_76[18]), .out19(out_76[19]),
    .out20(out_76[20]), .out21(out_76[21]), .out22(out_76[22]), .out23(out_76[23]), .out24(out_76[24]),
    .out25(out_76[25]), .out26(out_76[26]), .out27(out_76[27]), .out28(out_76[28]), .out29(out_76[29]),
    .out30(out_76[30]), .out31(out_76[31]), .in(in_1), .sel(in_2[4:0]), .en(decoder_1_out1));
  Decoder #(.disabled(0)) decoder_2 (.out0(decoder_2_out0), .out1(decoder_2_out1), .sel(in_4[5]), .en(in_6));
  Decoder #(.select(5), .disabled(0)) decoder_3 (
    .out0(out_79[0]), .out1(out_79[1]), .out2(out_79[2]), .out3(out_79[3]), .out4(out_79[4]),
    .out5(out_79[5]), .out6(out_79[6]), .out7(out_79[7]), .out8(out_79[8]), .out9(out_79[9]),
    .out10(out_79[10]), .out11(out_79[11]), .out12(out_79[12]), .out13(out_79[13]), .out14(out_79[14]),
    .out15(out_79[15]), .out16(out_79[16]), .out17(out_79[17]), .out18(out_79[18]), .out19(out_79[19]),
    .out20(out_79[20]), .out21(out_79[21]), .out22(out_79[22]), .out23(out_79[23]), .out24(out_79[24]),
    .out25(out_79[25]), .out26(out_79[26]), .out27(out_79[27]), .out28(out_79[28]), .out29(out_79[29]),
    .out30(out_79[30]), .out31(out_79[31]), .sel(in_4[4:0]), .en(decoder_2_out0));
  Decoder #(.select(5), .disabled(0)) decoder_4 (
    .out0(out_78[0]), .out1(out_78[1]), .out2(out_78[2]), .out3(out_78[3]), .out4(out_78[4]),
    .out5(out_78[5]), .out6(out_78[6]), .out7(out_78[7]), .out8(out_78[8]), .out9(out_78[9]),
    .out10(out_78[10]), .out11(out_78[11]), .out12(out_78[12]), .out13(out_78[13]), .out14(out_78[14]),
    .out15(out_78[15]), .out16(out_78[16]), .out17(out_78[17]), .out18(out_78[18]), .out19(out_78[19]),
    .out20(out_78[20]), .out21(out_78[21]), .out22(out_78[22]), .out23(out_78[23]), .out24(out_78[24]),
    .out25(out_78[25]), .out26(out_78[26]), .out27(out_78[27]), .out28(out_78[28]), .out29(out_78[29]),
    .out30(out_78[30]), .out31(out_78[31]), .sel(in_4[4:0]), .en(decoder_2_out1));
  Decoder #(.disabled(0)) decoder_5 (.out0(decoder_5_out0), .out1(decoder_5_out1), .sel(in_3[5]), .en(in_5));
  Multiplexer #(.select(5), .disabled(0)) multiplexer_1 (
    .in0(in_10[0]), .in1(in_10[1]), .in2(in_10[2]), .in3(in_10[3]), .in4(in_10[4]), .in5(in_10[5]),
    .in6(in_10[6]), .in7(in_10[7]), .in8(in_10[8]), .in9(in_10[9]), .in10(in_10[10]), .in11(in_10[11]),
    .in12(in_10[12]), .in13(in_10[13]), .in14(in_10[14]), .in15(in_10[15]), .in16(in_10[16]),
    .in17(in_10[17]), .in18(in_10[18]), .in19(in_10[19]), .in20(in_10[20]), .in21(in_10[21]),
    .in22(in_10[22]), .in23(in_10[23]), .in24(in_10[24]), .in25(in_10[25]), .in26(in_10[26]),
    .in27(in_10[27]), .in28(in_10[28]), .in29(in_10[29]), .in30(in_10[30]), .in31(in_10[31]),
    .out(multiplexer_1_out), .sel(in_3[4:0]), .en(decoder_5_out0));
  Multiplexer #(.select(5), .disabled(0)) multiplexer_2 (
    .in0(in_9[0]), .in1(in_9[1]), .in2(in_9[2]), .in3(in_9[3]), .in4(in_9[4]), .in5(in_9[5]), .in6(in_9[6]),
    .in7(in_9[7]), .in8(in_9[8]), .in9(in_9[9]), .in10(in_9[10]), .in11(in_9[11]), .in12(in_9[12]),
    .in13(in_9[13]), .in14(in_9[14]), .in15(in_9[15]), .in16(in_9[16]), .in17(in_9[17]), .in18(in_9[18]),
    .in19(in_9[19]), .in20(in_9[20]), .in21(in_9[21]), .in22(in_9[22]), .in23(in_9[23]), .in24(in_9[24]),
    .in25(in_9[25]), .in26(in_9[26]), .in27(in_9[27]), .in28(in_9[28]), .in29(in_9[29]), .in30(in_9[30]),
    .in31(in_9[31]), .out(multiplexer_2_out), .sel(in_3[4:0]), .en(decoder_5_out1));
  or or_1 (out_43, multiplexer_1_out, multiplexer_2_out);
  Button button_1 (.out(button_1_out));
  Counter #(.width(6), .max('h3f)) counter_1 (
    .load(1'b0), .D({6{1'b0}}), .count(in_8), .Q(counter_1_q), .clk(button_1_out), .clr(button_2_out));  // open: carry
  Button button_2 (.out(button_2_out));
  Decoder #(.disabled(0)) decoder_6 (.out0(decoder_6_out0), .out1(decoder_6_out1), .sel(counter_1_q[5]), .en(in_8));
  Decoder #(.select(5), .disabled(0)) decoder_7 (
    .out0(out_11), .out1(out_12), .out2(out_13), .out3(out_14), .out4(out_15), .out5(out_16), .out6(out_17),
    .out7(out_18), .out8(out_19), .out9(out_20), .out10(out_21), .out11(out_22), .out12(out_23),
    .out13(out_24), .out14(out_25), .out15(out_26), .out16(out_27), .out17(out_28), .out18(out_29),
    .out19(out_30), .out20(out_31), .out21(out_32), .out22(out_33), .out23(out_34), .out24(out_35),
    .out25(out_36), .out26(out_37), .out27(out_38), .out28(out_39), .out29(out_40), .out30(out_41),
    .out31(out_42), .sel(counter_1_q[4:0]), .en(decoder_6_out0));
  Decoder #(.select(5), .disabled(0)) decoder_8 (
    .out0(out_44), .out1(out_45), .out2(out_46), .out3(out_47), .out4(out_48), .out5(out_49), .out6(out_50),
    .out7(out_51), .out8(out_52), .out9(out_53), .out10(out_54), .out11(out_55), .out12(out_56),
    .out13(out_57), .out14(out_58), .out15(out_59), .out16(out_60), .out17(out_61), .out18(out_62),
    .out19(out_63), .out20(out_64), .out21(out_65), .out22(out_66), .out23(out_67), .out24(out_68),
    .out25(out_69), .out26(out_70), .out27(out_71), .out28(out_72), .out29(out_73), .out30(out_74),
    .out31(out_75), .sel(counter_1_q[4:0]), .en(decoder_6_out1));
endmodule

module main_aff (
  input  [3:0] in_1,
  input  [3:0] in_2,
  input  [3:0] in_3,
  input  in_4,
  input  [3:0] in_5,
  input  [3:0] in_6,
  input  in_7,
  input  [2:0] in_8,
  input  in_9
);

  wire [2:0] affh_1_ah_2;
  wire [3:0] affh_1_ah;
  wire [6:0] affh_2_ah, binairehexadigit_1_p2;

  Hex_Digit_Display hex_digit_display_1 (.value(in_3), .dp(in_7));
  _7_Segment_Display u_7_segment_display_1 (
    .g(affh_1_ah[3]), .f(affh_1_ah[2]), .a(affh_1_ah[1]), .b(affh_1_ah[0]), .e(affh_1_ah_2[2]),
    .d(affh_1_ah_2[1]), .c(affh_1_ah_2[0]), .dp(in_7));
  AFFH affh_1 (.V(in_3), .AH({affh_1_ah_2, affh_1_ah}));
  // BinaireHexaDigit binairehexadigit_1: pin names not known; wires that end beside it: in_2, binairehexadigit_1_p2
  AFFH affh_2 (.V(in_2), .AH(affh_2_ah));
  Hex_Digit_Display hex_digit_display_2 (.value(in_2), .dp(in_4));
  _7_Segment_Display u_7_segment_display_2 (
    .g(affh_2_ah[3]), .f(affh_2_ah[2]), .a(affh_2_ah[1]), .b(affh_2_ah[0]), .e(affh_2_ah[6]),
    .d(affh_2_ah[5]), .c(affh_2_ah[4]), .dp(in_4));
  _7_Segment_Display u_7_segment_display_3 (
    .g(binairehexadigit_1_p2[3]), .f(binairehexadigit_1_p2[2]), .a(binairehexadigit_1_p2[1]),
    .b(binairehexadigit_1_p2[0]), .e(binairehexadigit_1_p2[6]), .d(binairehexadigit_1_p2[5]),
    .c(binairehexadigit_1_p2[4]), .dp(in_4));
  LED led_1 (.in(affh_2_ah[2]));
  LED led_2 (.in(affh_2_ah[2]));
  LED led_3 (.in(affh_2_ah[2]));
  LED led_4 (.in(affh_2_ah[6]));
  LED led_5 (.in(affh_2_ah[6]));
  LED led_6 (.in(affh_2_ah[6]));
  LED led_7 (.in(binairehexadigit_1_p2[2]));
  LED led_8 (.in(binairehexadigit_1_p2[2]));
  LED led_9 (.in(binairehexadigit_1_p2[2]));
  LED led_10 (.in(binairehexadigit_1_p2[6]));
  LED led_11 (.in(binairehexadigit_1_p2[6]));
  LED led_12 (.in(binairehexadigit_1_p2[6]));
  LED led_13 (.in(affh_2_ah[1]));
  LED led_14 (.in(affh_2_ah[1]));
  LED led_15 (.in(affh_2_ah[1]));
  LED led_16 (.in(affh_2_ah[3]));
  LED led_17 (.in(affh_2_ah[3]));
  LED led_18 (.in(affh_2_ah[3]));
  LED led_19 (.in(affh_2_ah[5]));
  LED led_20 (.in(affh_2_ah[5]));
  LED led_21 (.in(affh_2_ah[5]));
  LED led_22 (.in(binairehexadigit_1_p2[1]));
  LED led_23 (.in(binairehexadigit_1_p2[1]));
  LED led_24 (.in(binairehexadigit_1_p2[1]));
  LED led_25 (.in(binairehexadigit_1_p2[3]));
  LED led_26 (.in(binairehexadigit_1_p2[3]));
  LED led_27 (.in(binairehexadigit_1_p2[3]));
  LED led_28 (.in(binairehexadigit_1_p2[5]));
  LED led_29 (.in(binairehexadigit_1_p2[5]));
  LED led_30 (.in(binairehexadigit_1_p2[5]));
  LED led_31 (.in(affh_2_ah[0]));
  LED led_32 (.in(affh_2_ah[0]));
  LED led_33 (.in(affh_2_ah[0]));
  LED led_34 (.in(affh_2_ah[4]));
  LED led_35 (.in(affh_2_ah[4]));
  LED led_36 (.in(affh_2_ah[4]));
  LED led_37 (.in(in_4));
  LED led_38 (.in(binairehexadigit_1_p2[0]));
  LED led_39 (.in(binairehexadigit_1_p2[0]));
  LED led_40 (.in(binairehexadigit_1_p2[0]));
  LED led_41 (.in(binairehexadigit_1_p2[4]));
  LED led_42 (.in(binairehexadigit_1_p2[4]));
  LED led_43 (.in(binairehexadigit_1_p2[4]));
  LED led_44 (.in(in_4));
  LED led_45 (.in(in_1[2]));
  LED led_46 (.in(in_1[2]));
  LED led_47 (.in(in_1[2]));
  LED led_48 (.in(in_5[3]));
  LED led_49 (.in(in_5[3]));
  LED led_50 (.in(in_5[3]));
  LED led_51 (.in(in_1[1]));
  LED led_52 (.in(in_1[1]));
  LED led_53 (.in(in_1[1]));
  LED led_54 (.in(in_1[3]));
  LED led_55 (.in(in_1[3]));
  LED led_56 (.in(in_1[3]));
  LED led_57 (.in(in_5[2]));
  LED led_58 (.in(in_5[2]));
  LED led_59 (.in(in_5[2]));
  LED led_60 (.in(in_6[1]));
  LED led_61 (.in(in_6[1]));
  LED led_62 (.in(in_6[1]));
  LED led_63 (.in(in_6[2]));
  LED led_64 (.in(in_6[2]));
  LED led_65 (.in(in_6[3]));
  LED led_66 (.in(in_6[3]));
  LED led_67 (.in(in_6[2]));
  LED led_68 (.in(in_6[3]));
  LED led_69 (.in(in_8[2]));
  LED led_70 (.in(in_8[2]));
  LED led_71 (.in(in_8[2]));
  LED led_72 (.in(in_8[1]));
  LED led_73 (.in(in_8[1]));
  LED led_74 (.in(in_8[1]));
  LED led_75 (.in(in_1[0]));
  LED led_76 (.in(in_1[0]));
  LED led_77 (.in(in_1[0]));
  LED led_78 (.in(in_5[1]));
  LED led_79 (.in(in_5[1]));
  LED led_80 (.in(in_5[1]));
  LED led_81 (.in(in_5[0]));
  LED led_82 (.in(in_6[0]));
  LED led_83 (.in(in_6[0]));
  LED led_84 (.in(in_6[0]));
  LED led_85 (.in(in_8[0]));
  LED led_86 (.in(in_8[0]));
  LED led_87 (.in(in_8[0]));
  LED led_88 (.in(in_9));

  // Notes on the sheet:
  //   other_chip8.circ
  //   other_chip8.circ
  //   Other.jar
endmodule

module DED0 (
  input  in_1,
  output Output_0,
  output Output_1
);

  not not_1 (Output_0, in_1);

  assign Output_1 = in_1;

  // Notes on the sheet:
  //   2 Transistors
endmodule

module DEDE (
  input  in_1,
  input  in_2,
  output Output_0,
  output Output_1
);

  wire not_1_out;

  not not_1 (not_1_out, in_1);
  and and_1 (Output_0, not_1_out, in_2);
  and and_2 (Output_1, in_1, in_2);

  // Notes on the sheet:
  //   2+6*2=2+12=14 Transistors
endmodule

module DEC0 (
  input  [1:0] SEL,
  output Output_0,
  output Output_1,
  output Output_2,
  output Output_3
);

  wire not_1_out, not_2_out;

  not not_1 (not_1_out, SEL[0]);
  not not_2 (not_2_out, SEL[1]);
  and and_1 (Output_0, not_1_out, not_2_out);
  and and_2 (Output_1, SEL[0], not_2_out);
  and and_3 (Output_2, not_1_out, SEL[1]);
  and and_4 (Output_3, SEL[0], SEL[1]);

  // Notes on the sheet:
  //   2*2+6*4=4+24=28 Transistors
endmodule

module DECE (
  input  [1:0] SEL,
  input  ENABLE,
  output Output_0,
  output Output_1,
  output Output_2,
  output Output_3
);

  wire and_1_out, and_3_out, and_5_out, and_7_out, not_1_out, not_2_out;

  not not_1 (not_1_out, SEL[1]);
  not not_2 (not_2_out, SEL[0]);
  and and_1 (and_1_out, not_2_out, not_1_out);
  and and_2 (Output_0, and_1_out, ENABLE);
  and and_3 (and_3_out, SEL[0], not_1_out);
  and and_4 (Output_1, and_3_out, ENABLE);
  and and_5 (and_5_out, not_2_out, SEL[1]);
  and and_6 (Output_2, and_5_out, ENABLE);
  and and_7 (and_7_out, SEL[0], SEL[1]);
  and and_8 (Output_3, and_7_out, ENABLE);
endmodule

module DE0E (
  input  [1:0] SEL,
  input  ENABLE,
  output Output_0,
  output Output_1,
  output Output_2,
  output Output_3
);

  wire dec0_1_output_0, dec0_1_output_1, dec0_1_output_2, dec0_1_output_3;

  DEC0 dec0_1 (
    .SEL(SEL), .Output_0(dec0_1_output_0), .Output_1(dec0_1_output_1), .Output_2(dec0_1_output_2),
    .Output_3(dec0_1_output_3));
  and and_1 (Output_0, dec0_1_output_0, ENABLE);
  and and_2 (Output_1, dec0_1_output_1, ENABLE);
  and and_3 (Output_2, dec0_1_output_2, ENABLE);
  and and_4 (Output_3, dec0_1_output_3, ENABLE);
endmodule

module DET0 (
  input  [1:0] SEL,
  output Output_0,
  output Output_1,
  output Output_2,
  output Output_3
);

  wire non_1_out_2, non_2_out_2;

  NON non_1 (.in_1(SEL[1]), .out_2(non_1_out_2));
  NON non_2 (.in_1(SEL[0]), .out_2(non_2_out_2));
  ET et_1 (.in_1(non_2_out_2), .in_2(non_1_out_2), .out_3(Output_0));
  ET et_2 (.in_1(SEL[0]), .in_2(non_1_out_2), .out_3(Output_1));
  ET et_3 (.in_1(non_2_out_2), .in_2(SEL[1]), .out_3(Output_2));
  ET et_4 (.in_1(SEL[0]), .in_2(SEL[1]), .out_3(Output_3));

  // Notes on the sheet:
  //   2*2+6*4=4+24=28 Transistors
endmodule

module DT0E (
  input  [1:0] SEL,
  input  ENABLE,
  output Output_0,
  output Output_1,
  output Output_2,
  output Output_3
);

  wire det0_1_output_0, det0_1_output_1, det0_1_output_2, det0_1_output_3;

  DET0 det0_1 (
    .SEL(SEL), .Output_0(det0_1_output_0), .Output_1(det0_1_output_1), .Output_2(det0_1_output_2),
    .Output_3(det0_1_output_3));
  ET et_1 (.in_1(det0_1_output_0), .in_2(ENABLE), .out_3(Output_0));
  ET et_2 (.in_1(det0_1_output_1), .in_2(ENABLE), .out_3(Output_1));
  ET et_3 (.in_1(det0_1_output_2), .in_2(ENABLE), .out_3(Output_2));
  ET et_4 (.in_1(det0_1_output_3), .in_2(ENABLE), .out_3(Output_3));

  // Notes on the sheet:
  //   28+6*4=28+24=52 Transistors
endmodule

module DT4E (
  input  in_1,
  input  [3:0] in_2,
  output Output_00,
  output Output_01,
  output Output_02,
  output Output_03,
  output Output_04,
  output Output_05,
  output Output_06,
  output Output_07,
  output Output_08,
  output Output_09,
  output Output_10,
  output Output_11,
  output Output_12,
  output Output_13,
  output Output_14,
  output Output_16
);

  wire dt0e_1_output_0, dt0e_1_output_1, dt0e_1_output_2, dt0e_1_output_3;

  DT0E dt0e_1 (
    .SEL(in_2[3:2]), .ENABLE(in_1), .Output_0(dt0e_1_output_0), .Output_1(dt0e_1_output_1),
    .Output_2(dt0e_1_output_2), .Output_3(dt0e_1_output_3));
  DT0E dt0e_2 (
    .SEL(in_2[1:0]), .ENABLE(dt0e_1_output_0), .Output_0(Output_00), .Output_1(Output_01),
    .Output_2(Output_02), .Output_3(Output_03));
  DT0E dt0e_3 (
    .SEL(in_2[1:0]), .ENABLE(dt0e_1_output_1), .Output_0(Output_04), .Output_1(Output_05),
    .Output_2(Output_06), .Output_3(Output_07));
  DT0E dt0e_4 (
    .SEL(in_2[1:0]), .ENABLE(dt0e_1_output_2), .Output_0(Output_08), .Output_1(Output_09),
    .Output_2(Output_10), .Output_3(Output_11));
  DT0E dt0e_5 (
    .SEL(in_2[1:0]), .ENABLE(dt0e_1_output_3), .Output_0(Output_12), .Output_1(Output_13),
    .Output_2(Output_14), .Output_3(Output_16));
endmodule

module DMXD (
  input  [1:0] SEL,
  input  ENABLE,
  input  Input,
  output Output_0,
  output Output_1,
  output Output_2,
  output Output_3
);

  wire and_1_out, and_2_out, and_3_out, and_4_out, and_5_out, and_6_out, and_7_out, and_8_out, not_1_out,
       not_2_out;

  not not_1 (not_1_out, SEL[0]);
  not not_2 (not_2_out, SEL[1]);
  and and_1 (and_1_out, not_1_out, not_2_out);
  and and_2 (and_2_out, SEL[0], not_2_out);
  and and_3 (and_3_out, not_1_out, SEL[1]);
  and and_4 (and_4_out, SEL[0], SEL[1]);
  and and_5 (and_5_out, and_1_out, ENABLE);
  and and_6 (and_6_out, and_2_out, ENABLE);
  and and_7 (and_7_out, and_3_out, ENABLE);
  and and_8 (and_8_out, and_4_out, ENABLE);
  and and_9 (Output_0, and_5_out, Input);
  and and_10 (Output_1, and_6_out, Input);
  and and_11 (Output_2, and_7_out, Input);
  and and_12 (Output_3, and_8_out, Input);

  // Notes on the sheet:
  //   52+1*(6*4)=52+1*24=52+24=76 Transistors
endmodule

module DMX1 (
  input  [1:0] Sel,
  input  ENABLE,
  input  Input,
  output Output_0,
  output Output_1,
  output Output_2,
  output Ouput_3
);

  wire de0e_1_output_0, de0e_1_output_1, de0e_1_output_2, de0e_1_output_3;

  DE0E de0e_1 (
    .SEL(Sel), .ENABLE(ENABLE), .Output_0(de0e_1_output_0), .Output_1(de0e_1_output_1),
    .Output_2(de0e_1_output_2), .Output_3(de0e_1_output_3));
  and and_1 (Output_0, de0e_1_output_0, Input);
  and and_2 (Output_1, de0e_1_output_1, Input);
  and and_3 (Output_2, de0e_1_output_2, Input);
  and and_4 (Ouput_3, de0e_1_output_3, Input);

  // Notes on the sheet:
  //   52+1*(6*4)=52+1*24=52+24=76 Transistors
endmodule

module DMX2 (
  input  [1:0] Sel,
  input  ENABLE,
  input  [1:0] Input,
  output [1:0] Output_0,
  output [1:0] Output_1,
  output [1:0] Output_2,
  output [1:0] Output_3
);

  wire de0e_1_output_0, de0e_1_output_1, de0e_1_output_2, de0e_1_output_3;

  DE0E de0e_1 (
    .SEL(Sel), .ENABLE(ENABLE), .Output_0(de0e_1_output_0), .Output_1(de0e_1_output_1),
    .Output_2(de0e_1_output_2), .Output_3(de0e_1_output_3));
  and and_1 (Output_0[0], de0e_1_output_0, Input[0]);
  and and_2 (Output_1[0], de0e_1_output_1, Input[0]);
  and and_3 (Output_2[0], de0e_1_output_2, Input[0]);
  and and_4 (Output_3[0], de0e_1_output_3, Input[0]);
  and and_5 (Output_0[1], de0e_1_output_0, Input[1]);
  and and_6 (Output_1[1], de0e_1_output_1, Input[1]);
  and and_7 (Output_2[1], de0e_1_output_2, Input[1]);
  and and_8 (Output_3[1], de0e_1_output_3, Input[1]);

  // Notes on the sheet:
  //   52+2*(6*4)=52+2*24=52+48=100 Transistors
endmodule

module MUXD (
  input  [1:0] Sel,
  input  ENABLE,
  input  Input_0,
  input  Input_1,
  input  Input_2,
  input  Input_3,
  output Ouput
);

  wire and_1_out, and_2_out, and_3_out, and_4_out, and_5_out, and_6_out, and_7_out, and_8_out, and_9_out,
       and_10_out, and_11_out, and_12_out, not_1_out, not_2_out, or_1_out, or_3_out;

  not not_1 (not_1_out, Sel[1]);
  not not_2 (not_2_out, Sel[0]);
  and and_1 (and_1_out, not_2_out, not_1_out);
  and and_2 (and_2_out, and_1_out, ENABLE);
  and and_3 (and_3_out, Sel[0], not_1_out);
  and and_4 (and_4_out, and_3_out, ENABLE);
  and and_5 (and_5_out, not_2_out, Sel[1]);
  and and_6 (and_6_out, and_5_out, ENABLE);
  and and_7 (and_7_out, Sel[0], Sel[1]);
  and and_8 (and_8_out, and_7_out, ENABLE);
  and and_9 (and_9_out, and_2_out, Input_0);
  and and_10 (and_10_out, and_4_out, Input_1);
  and and_11 (and_11_out, and_6_out, Input_2);
  and and_12 (and_12_out, and_8_out, Input_3);
  or or_1 (or_1_out, and_9_out, and_10_out);
  or or_2 (Ouput, or_1_out, or_3_out);
  or or_3 (or_3_out, and_11_out, and_12_out);

  // Notes on the sheet:
  //   52+1*(6*4+6*3)=52+1*(6*7)=52+1*42=52+42=94 Transistors
endmodule

module MUX1 (
  input  [1:0] Sel,
  input  ENABLE,
  input  Input_0,
  input  Input_1,
  input  Input_2,
  input  Input_3,
  output Ouput
);

  wire and_1_out, and_2_out, and_3_out, and_4_out, dece_1_output_0, dece_1_output_1, dece_1_output_2,
       dece_1_output_3;

  DECE dece_1 (
    .SEL(Sel), .ENABLE(ENABLE), .Output_0(dece_1_output_0), .Output_1(dece_1_output_1),
    .Output_2(dece_1_output_2), .Output_3(dece_1_output_3));
  and and_1 (and_1_out, dece_1_output_0, Input_0);
  and and_2 (and_2_out, dece_1_output_1, Input_1);
  and and_3 (and_3_out, dece_1_output_2, Input_2);
  and and_4 (and_4_out, dece_1_output_3, Input_3);
  or or_1 (Ouput, and_1_out, and_2_out, and_3_out, and_4_out);

  // Notes on the sheet:
  //   52+1*(6*4+6*3)=52+1*(6*7)=52+1*42=52+42=94 Transistors
endmodule

module MUX2 (
  input  [1:0] Sel,
  input  ENABLE,
  input  [1:0] Input_0,
  input  [1:0] Input_1,
  input  [1:0] Input_2,
  input  [1:0] Input_3,
  output [1:0] Output
);

  wire and_1_out, and_2_out, and_3_out, and_4_out, and_5_out, and_6_out, and_7_out, and_8_out,
       dece_1_output_0, dece_1_output_1, dece_1_output_2, dece_1_output_3;

  DECE dece_1 (
    .SEL(Sel), .ENABLE(ENABLE), .Output_0(dece_1_output_0), .Output_1(dece_1_output_1),
    .Output_2(dece_1_output_2), .Output_3(dece_1_output_3));
  and and_1 (and_1_out, dece_1_output_0, Input_0[0]);
  and and_2 (and_2_out, dece_1_output_1, Input_1[0]);
  and and_3 (and_3_out, dece_1_output_2, Input_2[0]);
  and and_4 (and_4_out, dece_1_output_3, Input_3[0]);
  and and_5 (and_5_out, dece_1_output_0, Input_0[1]);
  and and_6 (and_6_out, dece_1_output_1, Input_1[1]);
  and and_7 (and_7_out, dece_1_output_2, Input_2[1]);
  and and_8 (and_8_out, dece_1_output_3, Input_3[1]);
  or or_1 (Output[0], and_1_out, and_2_out, and_3_out, and_4_out);
  or or_2 (Output[1], and_5_out, and_6_out, and_7_out, and_8_out);

  // Notes on the sheet:
  //   52+2*(6*4+6*3)=52+2*(6*7)=52+2*42=52+84=136 Transistors
endmodule

module CODV (
  input  Input_0,
  input  Input_1,
  input  Input_2,
  input  Input_3,
  input  Input_4,
  input  Input_5,
  input  Input_6,
  input  Input_7,
  input  Input_8,
  input  Input_9,
  input  Input_10,
  input  Input_11,
  input  Input_12,
  input  Input_13,
  input  Input_14,
  input  Input_15,
  input  Input_16,
  input  Input_17,
  input  Input_18,
  input  Input_19,
  input  Input_20,
  input  Input_21,
  input  Input_22,
  input  Input_23,
  input  Input_24,
  input  Input_25,
  input  Input_26,
  input  Input_27,
  input  Input_28,
  input  Input_29,
  input  Input_30,
  input  Input_31,
  input  Enable,
  output Validate,
  output [4:0] Output
);

  wire and_1_out, codh_1_validate, not_1_out;
  wire [3:0] codh_1_output, codh_2_output;

  CODH codh_1 (
    .Enable(and_1_out), .Validate(codh_1_validate), .Output(codh_1_output), .Input_0(Input_0),
    .Input_1(Input_1), .Input_2(Input_2), .Input_3(Input_3), .Input_4(Input_4), .Input_5(Input_5),
    .Input_6(Input_6), .Input_7(Input_7), .Input_8(Input_8), .Input_9(Input_9), .Input_10(Input_10),
    .Input_11(Input_11), .Input_12(Input_12), .Input_13(Input_13), .Input_14(Input_14), .Input_15(Input_15));
  CODH codh_2 (
    .Enable(Enable), .Validate(Output[4]), .Output(codh_2_output), .Input_0(Input_16), .Input_1(Input_17),
    .Input_2(Input_18), .Input_3(Input_19), .Input_4(Input_20), .Input_5(Input_21), .Input_6(Input_22),
    .Input_7(Input_23), .Input_8(Input_24), .Input_9(Input_25), .Input_10(Input_26), .Input_11(Input_27),
    .Input_12(Input_28), .Input_13(Input_29), .Input_14(Input_30), .Input_15(Input_31));
  assign Output[3:0] = codh_1_output | codh_2_output;  // OR_Gate or_1, 4 bits wide
  or or_2 (Validate, codh_1_validate, Output[4]);
  not not_1 (not_1_out, Output[4]);
  and and_1 (and_1_out, not_1_out, Enable);

  // Notes on the sheet:
  //   other_chip8.circ
  //   other_chip8.circ
endmodule
