// Logisim project 07_FLIP_FLOP_00_V.circ as structural Verilog: 15 circuits, main circuit main
module main (
  input  S,
  input  Clock,
  input  R,
  input  D,
  input  Clock_2,
  input  J,
  input  J_2,
  input  K,
  input  K_2,
  input  Clock_3,
  input  Clock_4,
  input  Clock_5,
  input  Clock_6,
  input  D_2,
  input  D_3,
  input  S_2,
  input  R_2,
  output out_18,
  output out_19,
  output out_20,
  output out_21,
  output out_22,
  output out_23,
  output out_24,
  output out_25,
  output out_26,
  output out_27,
  output out_28,
  output out_29,
  output out_30,
  output out_31
);

  S_R_Flip_Flop #(.trigger("high")) s_r_ff_1 (
    .S(S), .clk(Clock_2), .R(R), .Q(out_18), .preset(1'b0), .reset(1'b0), .en(1'b1));  // open: Qn
  J_K_Flip_Flop #(.trigger("falling")) j_k_ff_1 (
    .J(J), .clk(Clock_3), .K(K), .Q(out_22), .preset(1'b0), .en(1'b1), .reset(1'b0));  // open: Qn
  D_Flip_Flop #(.trigger("falling")) d_ff_1 (
    .clk(Clock_5), .D(D_2), .Q(out_26), .preset(1'b0), .en(1'b1), .reset(1'b0));  // open: Qn
  S_R_Flip_Flop #(.trigger("high")) s_r_ff_2 (
    .S(S_2), .clk(1'b1), .R(R_2), .Q(out_30), .preset(1'b0), .reset(1'b0), .en(1'b1));  // open: Qn
  RSH rsh_1 (.S(S), .H(Clock_2), .R(R), .Q(out_19));  // open: Q_Not
  JKD jkd_1 (.J(J), .CLK(Clock_3), .K(K), .Q(out_23));  // open: QN
  DD dd_1 (.D(D_2), .H(Clock_5), .Q(out_27));  // open: QN
  RS rs_1 (.R(R_2), .Q(out_31), .S(S_2));  // open: Q_Not
  D_Flip_Flop #(.trigger("high")) d_ff_2 (
    .clk(Clock), .D(D), .Q(out_20), .preset(1'b0), .en(1'b1), .reset(1'b0));  // open: Qn
  J_K_Flip_Flop j_k_ff_2 (
    .J(J_2), .clk(Clock_4), .K(K_2), .Q(out_24), .preset(1'b0), .en(1'b1), .reset(1'b0));  // open: Qn
  D_Flip_Flop d_ff_3 (.clk(Clock_6), .D(D_3), .Q(out_28), .preset(1'b0), .en(1'b1), .reset(1'b0));  // open: Qn
  D d_1 (.D(D), .H(Clock), .Q(out_21));  // open: Q_Not
  JKM jkm_1 (.J(J_2), .CLK(Clock_4), .K(K_2), .Q(out_25));  // open: QN
  DM dm_1 (.D(D_3), .Q(out_29), .H(Clock_6));  // open: QN
endmodule

module main_tr (
  input  S,
  input  Clock,
  input  R,
  input  D,
  output out_5,
  output out_6,
  output out_7,
  output out_8
);

  S_R_Flip_Flop #(.trigger("high")) s_r_ff_1 (
    .S(S), .clk(1'b1), .R(R), .Q(out_5), .preset(1'b0), .reset(1'b0), .en(1'b1));  // open: Qn
  RSTR rstr_1 (.S(S), .R(R), .Q(out_6));  // open: Q_Not
  D_Flip_Flop #(.trigger("high")) d_ff_1 (
    .clk(Clock), .D(D), .Q(out_7), .preset(1'b0), .en(1'b1), .reset(1'b0));  // open: Qn
  DTR dtr_1 (.D(D), .Clock(Clock), .Q(out_8));  // open: Q_Not
endmodule

module RS (
  input  R,
  input  S,
  output Q,
  output Q_Not
);

  nor nor_1 (Q, R, Q_Not);
  nor nor_2 (Q_Not, Q, S);
endmodule

module RS1 (
  input  R,
  input  S,
  output Q,
  output Q_Not
);

  wire not_1_out, not_2_out;

  not not_1 (not_1_out, R);
  nand nand_1 (Q, not_1_out, Q_Not);
  nand nand_2 (Q_Not, Q, not_2_out);
  not not_2 (not_2_out, S);
endmodule

module RSL (
  input  S,
  input  R,
  output Q,
  output Q_Not
);

  wire and_1_out, not_1_out;

  not not_1 (not_1_out, R);
  and and_1 (and_1_out, S, not_1_out);
  RS rs_1 (.R(R), .Q(Q), .Q_Not(Q_Not), .S(and_1_out));

  // Notes on the sheet:
  //   S0
  //   R0
endmodule

module RSH (
  input  S,
  input  H,
  input  R,
  output Q,
  output Q_Not
);

  wire and_1_out, and_2_out;

  and and_1 (and_1_out, S, H);
  and and_2 (and_2_out, H, R);
  RS rs_1 (.R(and_2_out), .Q(Q), .Q_Not(Q_Not), .S(and_1_out));

  // Notes on the sheet:
  //   S0
  //   R0
endmodule

module RSHB (
  input  S,
  input  H,
  input  R,
  output Q,
  output Q_Not
);

  wire not_1_out;

  not not_1 (not_1_out, H);
  RSH rsh_1 (.S(S), .H(not_1_out), .R(R), .Q(Q), .Q_Not(Q_Not));

  // Notes on the sheet:
  //   S: pull=down
  //   R: pull=down
  //   H: pull=down
endmodule

module RSHB1 (
  input  S,
  input  H,
  input  R,
  output Q,
  output Q_Not
);

  wire and_1_out, and_2_out, not_1_out;

  and and_1 (and_1_out, S, not_1_out);
  not not_1 (not_1_out, H);
  and and_2 (and_2_out, not_1_out, R);
  RS rs_1 (.R(and_2_out), .Q(Q), .Q_Not(Q_Not), .S(and_1_out));

  // Notes on the sheet:
  //   S0
  //   R0
endmodule

module D (
  input  D,
  input  H,
  output Q,
  output Q_Not
);

  wire not_1_out;

  RSH rsh_1 (.S(D), .H(H), .R(not_1_out), .Q(Q), .Q_Not(Q_Not));
  not not_1 (not_1_out, D);

  // Notes on the sheet:
  //   S0
  //   R0
endmodule

module JKD (
  input  J,
  input  CLK,
  input  K,
  output Q,
  output QN
);

  wire not_1_out, rsh_1_q, rsh_1_q_not;

  not not_1 (not_1_out, CLK);
  RSH rsh_1 (.S(J), .H(CLK), .R(K), .Q(rsh_1_q), .Q_Not(rsh_1_q_not));
  RSH rsh_2 (.S(rsh_1_q), .H(not_1_out), .R(rsh_1_q_not), .Q(Q), .Q_Not(QN));

  // Notes on the sheet:
  //   H1
  //   S1
  //   R1
  //   H2
  //   S2
  //   Q1
  //   R2
  //   RSH1
  //   Q2
  //   RSH2
endmodule

module JKM (
  input  J,
  input  CLK,
  input  K,
  output Q,
  output QN
);

  wire not_1_out, rsh_1_q, rsh_1_q_not;

  not not_1 (not_1_out, CLK);
  RSH rsh_1 (.S(J), .H(not_1_out), .R(K), .Q(rsh_1_q), .Q_Not(rsh_1_q_not));
  RSH rsh_2 (.S(rsh_1_q), .H(CLK), .R(rsh_1_q_not), .Q(Q), .Q_Not(QN));

  // Notes on the sheet:
  //   S1
  //   R1
  //   H1
  //   RSH1
  //   Q1
  //   S2
  //   R2
  //   H2
  //   RSH2
  //   Q2
endmodule

module DD (
  input  D,
  input  H,
  output Q,
  output QN
);

  wire not_1_out;

  not not_1 (not_1_out, D);
  JKD jkd_1 (.J(D), .CLK(H), .K(not_1_out), .Q(Q), .QN(QN));
endmodule

module DM (
  input  D,
  input  H,
  output Q,
  output QN
);

  wire not_1_out;

  not not_1 (not_1_out, D);
  JKM jkm_1 (.J(D), .CLK(H), .K(not_1_out), .Q(Q), .QN(QN));
endmodule

module RSTR (
  input  S,
  input  R,
  output Q,
  output Q_Not
);

  wire transistor_1_out, transistor_3_out, transistor_5_out, transistor_7_out;

  Transistor #(.gate("br")) transistor_1 (.in(1'b1), .out(transistor_1_out), .gate(Q));
  Pull_Resistor pull_resistor_1 (.node(transistor_1_out));
  Transistor transistor_2 (.in(transistor_1_out), .out(Q_Not), .gate(S));
  Transistor #(.\type ("n")) transistor_3 (.in(Q_Not), .out(transistor_3_out), .gate(S));
  Transistor #(.\type ("n"), .gate("br")) transistor_4 (.in(Q_Not), .out(transistor_3_out), .gate(Q));
  Pull_Resistor pull_resistor_2 (.node(Q_Not));
  Pull_Resistor pull_resistor_3 (.node(Q));
  Transistor transistor_5 (.in(1'b1), .out(transistor_5_out), .gate(Q_Not));
  Pull_Resistor pull_resistor_4 (.node(transistor_5_out));
  Transistor #(.gate("br")) transistor_6 (.in(transistor_5_out), .out(Q), .gate(R));
  Transistor #(.\type ("n"), .gate("br")) transistor_7 (.in(Q), .out(transistor_7_out), .gate(R));
  Transistor #(.\type ("n")) transistor_8 (.in(Q), .out(transistor_7_out), .gate(Q_Not));
  // also tied to GND on the sheet: {transistor_3_out, transistor_7_out}

  // Notes on the sheet:
  //   NON-OU
  //   NON-OU
endmodule

module DTR (
  input  D,
  input  Clock,
  output Q,
  output Q_Not
);

  wire transistor_1_out, transistor_2_out, transistor_3_out, transistor_5_out, transistor_6_out,
       transistor_9_out, transistor_11_out, transistor_13_out;

  Transistor transistor_1 (.in(1'b1), .out(transistor_1_out), .gate(D));
  Pull_Resistor pull_resistor_1 (.node(transistor_1_out));
  Transistor #(.\type ("n")) transistor_2 (.in(transistor_1_out), .out(transistor_2_out), .gate(D));
  Transistor transistor_3 (.in(1'b1), .out(transistor_3_out), .gate(D));
  Pull_Resistor pull_resistor_2 (.node(transistor_3_out));
  Transistor #(.gate("br")) transistor_4 (.in(transistor_3_out), .out(Q_Not), .gate(Q));
  Transistor #(.\type ("n"), .gate("br")) transistor_5 (.in(Q_Not), .out(transistor_5_out), .gate(Q));
  Transistor #(.\type ("n")) transistor_6 (.in(Q_Not), .out(transistor_6_out), .gate(D));
  Pull_Resistor pull_resistor_3 (.node(transistor_6_out));
  Transistor #(.\type ("n")) transistor_7 (.in(transistor_6_out), .out(transistor_5_out), .gate(Clock));
  Transistor #(.gate("br")) transistor_8 (.in(1'b1), .out(transistor_3_out), .gate(Clock));
  Transistor transistor_9 (.in(1'b1), .out(transistor_9_out), .gate(Clock));
  Transistor transistor_10 (.in(transistor_9_out), .out(Q), .gate(Q_Not));
  Transistor #(.\type ("n")) transistor_11 (.in(Q), .out(transistor_11_out), .gate(Q_Not));
  Transistor #(.gate("br")) transistor_12 (.in(1'b1), .out(transistor_9_out), .gate(transistor_1_out));
  Pull_Resistor pull_resistor_4 (.node(transistor_9_out));
  Pull_Resistor pull_resistor_5 (.node(Q));
  Transistor #(.\type ("n"), .gate("br")) transistor_13 (.in(Q), .out(transistor_13_out), .gate(transistor_1_out));
  Pull_Resistor pull_resistor_6 (.node(transistor_13_out));
  Transistor #(.\type ("n"), .gate("br")) transistor_14 (.in(transistor_13_out), .out(transistor_11_out), .gate(Clock));
  Pull_Resistor pull_resistor_7 (.node(Q_Not));
  // also tied to GND on the sheet: {transistor_2_out, transistor_5_out, transistor_11_out}
endmodule
