// Logisim project 09_COUNTER_V.circ as structural Verilog: 22 circuits, main circuit main
module main (
  input  Load,
  input  Count,
  input  Clock,
  input  Clear,
  input  [3:0] Data,
  input  Load_2,
  input  Count_2,
  input  Clock_2,
  input  Clear_2,
  input  [3:0] Data_2,
  input  Count_3,
  input  Clock_3,
  input  Clear_3,
  output [3:0] out_14,
  output [3:0] out_15,
  output [3:0] out_16,
  output [3:0] out_17,
  output [3:0] out_18,
  output out_19,
  output out_20,
  output out_21,
  output out_22,
  output out_23,
  output [3:0] out_24,
  output [3:0] out_25,
  output [3:0] out_26,
  output [3:0] out_27,
  output [3:0] out_28,
  output out_29,
  output out_30,
  output out_31,
  output out_32,
  output out_33,
  output [3:0] out_34,
  output out_35
);

  wire not_1_out;

  Counter #(.width(4), .max('hf)) counter_1 (
    .load(Load), .D(Data), .count(Count), .Q(out_14), .carry(out_19), .clk(Clock), .clr(Clear));
  Counter #(.width(4), .max('hf)) counter_2 (
    .load(Load_2), .D(Data_2), .count(Count_2), .Q(out_24), .carry(out_29), .clk(Clock_2), .clr(Clear_2));
  CMP4_2 cmp4_2_1 (.Clock(Clock_3), .Count(Count_3), .Clear(Clear_3), .Output(out_34), .Carry(out_35));
  // Probe on out_14
  // Probe on out_14
  // Probe on out_14
  // Probe on out_24
  // Probe on out_24
  // Probe on out_24
  // Probe on out_34
  // Probe on out_34
  // Probe on out_34
  DCMP4D dcmp4d_1 (
    .Output(out_15), .Clock(Clock), .Carry(out_20), .Count(Count), .Clear(Clear), .Choice(Load), .Data(Data));
  CMP4D cmp4d_1 (
    .Output(out_25), .Clock(Clock_2), .Carry(out_30), .Count(Count_2), .Clear(Clear_2), .Choice(Load_2),
    .Data(Data_2));
  // Probe on out_15
  // Probe on out_15
  // Probe on out_15
  // Probe on out_25
  // Probe on out_25
  // Probe on out_25
  DMP4D2 dmp4d2_1 (
    .Clock(Clock), .Count(Count), .Clear(Clear), .Choice(Load), .in_5(Data), .Output(out_16), .Carry(out_21));
  CMP4D2 cmp4d2_1 (
    .Output(out_26), .Clock(Clock_2), .Carry(out_31), .Count(Count_2), .Clear(Clear_2), .Choice(Load_2),
    .Data(Data_2));
  // Probe on out_16
  // Probe on out_16
  // Probe on out_16
  // Probe on out_26
  // Probe on out_26
  // Probe on out_26
  Counter #(.width(4), .max('hf)) counter_3 (
    .load(1'b1), .D(4'b0000), .count(Count), .Q(out_17), .carry(out_22), .clk(Clock), .clr(Clear));
  // Probe on out_17
  // Probe on out_17
  // Probe on out_17
  Counter #(.width(4), .max('hf)) counter_4 (
    .load(1'b0), .D(4'b0000), .count(Count_2), .Q(out_27), .carry(out_32), .clk(Clock_2), .clr(Clear_2));
  // Probe on out_27
  // Probe on out_27
  // Probe on out_27
  DCMP4 dcmp4_1 (.Clock(Clock), .Count(Count), .Clear(Clear), .Output(out_18), .Carry(out_23));
  CMP4 cmp4_1 (.Clock(not_1_out), .Count(Count_2), .Clear(Clear_2), .Output(out_28), .Carry(out_33));
  not not_1 (not_1_out, Clock_2);
  // Probe on out_18
  // Probe on out_18
  // Probe on out_18
  // Probe on out_28
  // Probe on out_28
  // Probe on out_28
endmodule

module main1 (
  input  Load,
  input  Count,
  input  Clock,
  input  Clear,
  input  [3:0] Data,
  input  Load_2,
  input  Count_2,
  input  Clock_2,
  input  Clear_2,
  input  [7:0] Data_2,
  output [3:0] out_11,
  output [3:0] out_12,
  output [3:0] out_13,
  output [3:0] out_14,
  output out_15,
  output out_16,
  output out_17,
  output out_18,
  output [7:0] out_19,
  output [7:0] out_20,
  output [7:0] out_21,
  output [7:0] out_22,
  output out_23,
  output out_24,
  output out_25,
  output out_26
);

  Counter #(.width(4), .max('hf)) counter_1 (
    .load(Load), .D(Data), .count(Count), .Q(out_11), .carry(out_15), .clk(Clock), .clr(Clear));
  Counter counter_2 (
    .load(Load_2), .D(Data_2), .count(Count_2), .Q(out_19), .carry(out_23), .clk(Clock_2), .clr(Clear_2));
  // Probe on out_11
  // Probe on out_11
  // Probe on out_11
  // Probe on out_19
  // Probe on out_19
  // Probe on out_19
  DCP4D2 dcp4d2_1 (
    .Clock(Clock), .Count(Count), .Clear(Clear), .Choice(Load), .Data(Data), .Output(out_12), .Carry(out_16));
  // Probe on out_12
  // Probe on out_12
  // Probe on out_12
  // Probe on out_20
  DCP8D3 dcp8d3_1 (
    .Clock(Clock_2), .Count(Count_2), .Clear(Clear_2), .Choice(Load_2), .Data(Data_2), .Output(out_20),
    .Carry(out_24));
  // Probe on out_20
  // Probe on out_20
  DCP4D3 dcp4d3_1 (
    .Clock(Clock), .Count(Count), .Clear(Clear), .Choice(Load), .Data(Data), .Output(out_13), .Carry(out_17));
  // Probe on out_13
  // Probe on out_13
  // Probe on out_13
  DCP8D4 dcp8d4_1 (
    .Clock(Clock_2), .Count(Count_2), .Clear(Clear_2), .Choice(Load_2), .Data(Data_2), .Output(out_21),
    .Carry(out_25));
  DCP4D4 dcp4d4_1 (
    .Clock(Clock), .Count(Count), .Clear(Clear), .Choice(Load), .Data(Data), .Output(out_14), .Carry(out_18));
  // Probe on out_21
  // Probe on out_21
  // Probe on out_21
  // Probe on out_14
  // Probe on out_14
  // Probe on out_14
  DCP8D5 dcp8d5_1 (
    .Clock(Clock_2), .Count(Count_2), .Clear(Clear_2), .Choice(Load_2), .Data(Data_2), .Output(out_22),
    .Carry(out_26));
  // Probe on out_22
  // Probe on out_22
  // Probe on out_22
endmodule

module CMP4 (
  input  Clock,
  input  Count,
  input  Clear,
  output [3:0] Output,
  output Carry
);

  wire d_ff_1_qn, d_ff_2_qn, d_ff_3_qn, d_ff_4_qn;

  D_Flip_Flop #(.trigger("falling")) d_ff_1 (
    .clk(Clock), .D(d_ff_1_qn), .Q(Output[0]), .Qn(d_ff_1_qn), .preset(1'b0), .en(Count), .reset(Clear));
  D_Flip_Flop #(.trigger("falling")) d_ff_2 (
    .clk(Output[1]), .D(d_ff_2_qn), .Q(Output[2]), .Qn(d_ff_2_qn), .preset(1'b0), .en(Count), .reset(Clear));
  D_Flip_Flop #(.trigger("falling")) d_ff_3 (
    .clk(Output[0]), .D(d_ff_3_qn), .Q(Output[1]), .Qn(d_ff_3_qn), .preset(1'b0), .en(Count), .reset(Clear));
  D_Flip_Flop #(.trigger("falling")) d_ff_4 (
    .clk(Output[2]), .D(d_ff_4_qn), .Q(Carry), .Qn(d_ff_4_qn), .preset(1'b0), .en(Count), .reset(Clear));

  assign Output[3] = Carry;

  // Notes on the sheet:
  //   D0
  //   Q0
  //   D1
  //   Q1
  //   Q2
  //   D2
  //   Q3
  //   D3
endmodule

module CMP4_2 (
  input  Clock,
  input  Count,
  input  Clear,
  output [3:0] Output,
  output Carry
);

  wire d_ff_1_qn, d_ff_2_qn, d_ff_3_qn, d_ff_4_qn, not_1_out;

  D_Flip_Flop #(.trigger("falling")) d_ff_1 (
    .clk(not_1_out), .D(d_ff_1_qn), .Q(Output[0]), .Qn(d_ff_1_qn), .preset(1'b0), .en(Count), .reset(Clear));
  not not_1 (not_1_out, Clock);
  D_Flip_Flop #(.trigger("falling")) d_ff_2 (
    .clk(Output[0]), .D(d_ff_2_qn), .Q(Output[1]), .Qn(d_ff_2_qn), .preset(1'b0), .en(Count), .reset(Clear));
  D_Flip_Flop #(.trigger("falling")) d_ff_3 (
    .clk(Output[1]), .D(d_ff_3_qn), .Q(Output[2]), .Qn(d_ff_3_qn), .preset(1'b0), .en(Count), .reset(Clear));
  D_Flip_Flop #(.trigger("falling")) d_ff_4 (
    .clk(Output[2]), .D(d_ff_4_qn), .Q(Carry), .Qn(d_ff_4_qn), .preset(1'b0), .en(Count), .reset(Clear));

  assign Output[3] = Carry;

  // Notes on the sheet:
  //   Q0
  //   D1
  //   D0
  //   Q1
  //   D2
  //   Q2
  //   D3
  //   Q3
endmodule

module DCMP4 (
  input  Clock,
  input  Count,
  input  Clear,
  output [3:0] Output,
  output Carry
);

  wire d_ff_1_qn, d_ff_2_qn, d_ff_3_qn, d_ff_4_qn;

  D_Flip_Flop d_ff_1 (
    .clk(Clock), .D(d_ff_1_qn), .Q(Output[0]), .Qn(d_ff_1_qn), .preset(1'b0), .en(Count), .reset(Clear));
  D_Flip_Flop d_ff_2 (
    .clk(Output[0]), .D(d_ff_2_qn), .Q(Output[1]), .Qn(d_ff_2_qn), .preset(1'b0), .en(Count), .reset(Clear));
  D_Flip_Flop d_ff_3 (
    .clk(Output[2]), .D(d_ff_3_qn), .Q(Carry), .Qn(d_ff_3_qn), .preset(1'b0), .en(Count), .reset(Clear));
  D_Flip_Flop d_ff_4 (
    .clk(Output[1]), .D(d_ff_4_qn), .Q(Output[2]), .Qn(d_ff_4_qn), .preset(1'b0), .en(Count), .reset(Clear));

  assign Output[3] = Carry;

  // Notes on the sheet:
  //   D0
  //   Q0
  //   D1
  //   Q1
  //   D2
  //   Q3
  //   Q2
  //   D3
endmodule

module CMP4D (
  input  Clock,
  input  Count,
  input  Clear,
  input  Choice,
  input  [3:0] Data,
  output [3:0] Output,
  output Carry
);

  wire and_3_out, and_4_out, d_ff_1_qn, d_ff_2_qn, d_ff_3_qn, d_ff_4_qn, not_1_out, not_2_out, not_3_out,
       not_5_out, or_1_out, or_2_out, or_3_out, or_4_out;
  wire [3:0] and_1_out, and_2_out, bit_extender_1_out, not_4_out;

  not not_1 (not_1_out, and_4_out);
  not not_2 (not_2_out, Clear);
  not not_3 (not_3_out, Count);
  assign bit_extender_1_out = {{3{and_4_out}}, and_4_out};  // Bit_Extender bit_extender_1
  assign and_1_out = bit_extender_1_out & Data;  // AND_Gate and_1, 4 bits wide
  assign and_2_out = bit_extender_1_out & not_4_out;  // AND_Gate and_2, 4 bits wide
  assign not_4_out = ~Data;  // NOT_Gate not_4, 4 bits wide
  not not_5 (not_5_out, Clock);
  and and_3 (and_3_out, Clear, not_1_out);
  and and_4 (and_4_out, Clock, not_2_out, Choice, not_3_out);
  D_Flip_Flop #(.trigger("falling")) d_ff_1 (
    .clk(not_5_out), .D(d_ff_1_qn), .Q(Output[0]), .Qn(d_ff_1_qn), .preset(and_1_out[0]), .en(Count),
    .reset(or_2_out));
  or or_1 (or_1_out, and_3_out, and_2_out[1]);
  or or_2 (or_2_out, and_3_out, and_2_out[0]);
  D_Flip_Flop #(.trigger("falling")) d_ff_2 (
    .clk(Output[0]), .D(d_ff_2_qn), .Q(Output[1]), .Qn(d_ff_2_qn), .preset(and_1_out[1]), .en(Count),
    .reset(or_1_out));
  or or_3 (or_3_out, and_3_out, and_2_out[2]);
  D_Flip_Flop #(.trigger("falling")) d_ff_3 (
    .clk(Output[1]), .D(d_ff_3_qn), .Q(Output[2]), .Qn(d_ff_3_qn), .preset(and_1_out[2]), .en(Count),
    .reset(or_3_out));
  D_Flip_Flop #(.trigger("falling")) d_ff_4 (
    .clk(Output[2]), .D(d_ff_4_qn), .Q(Carry), .Qn(d_ff_4_qn), .preset(and_1_out[3]), .en(Count),
    .reset(or_4_out));
  or or_4 (or_4_out, and_3_out, and_2_out[3]);

  assign Output[3] = Carry;
endmodule

module DCMP4D (
  input  Clock,
  input  Count,
  input  Clear,
  input  Choice,
  input  [3:0] Data,
  output [3:0] Output,
  output Carry
);

  wire and_3_out, and_4_out, d_ff_1_qn, d_ff_2_qn, d_ff_3_qn, d_ff_4_qn, not_1_out, not_2_out, not_3_out,
       or_1_out, or_2_out, or_3_out, or_4_out;
  wire [3:0] and_1_out, and_2_out, bit_extender_1_out, not_4_out;

  not not_1 (not_1_out, and_4_out);
  not not_2 (not_2_out, Clear);
  not not_3 (not_3_out, Count);
  assign bit_extender_1_out = {{3{and_4_out}}, and_4_out};  // Bit_Extender bit_extender_1
  assign and_1_out = bit_extender_1_out & Data;  // AND_Gate and_1, 4 bits wide
  assign and_2_out = bit_extender_1_out & not_4_out;  // AND_Gate and_2, 4 bits wide
  assign not_4_out = ~Data;  // NOT_Gate not_4, 4 bits wide
  and and_3 (and_3_out, Clear, not_1_out);
  and and_4 (and_4_out, Clock, not_2_out, Choice, not_3_out);
  D_Flip_Flop d_ff_1 (
    .clk(Clock), .D(d_ff_1_qn), .Q(Output[0]), .Qn(d_ff_1_qn), .preset(and_1_out[0]), .en(Count),
    .reset(or_1_out));
  or or_1 (or_1_out, and_3_out, and_2_out[0]);
  or or_2 (or_2_out, and_3_out, and_2_out[1]);
  D_Flip_Flop d_ff_2 (
    .clk(Output[0]), .D(d_ff_2_qn), .Q(Output[1]), .Qn(d_ff_2_qn), .preset(and_1_out[1]), .en(Count),
    .reset(or_2_out));
  or or_3 (or_3_out, and_3_out, and_2_out[2]);
  D_Flip_Flop d_ff_3 (
    .clk(Output[1]), .D(d_ff_3_qn), .Q(Output[2]), .Qn(d_ff_3_qn), .preset(and_1_out[2]), .en(Count),
    .reset(or_3_out));
  D_Flip_Flop d_ff_4 (
    .clk(Output[2]), .D(d_ff_4_qn), .Q(Carry), .Qn(d_ff_4_qn), .preset(and_1_out[3]), .en(Count),
    .reset(or_4_out));
  or or_4 (or_4_out, and_3_out, and_2_out[3]);

  assign Output[3] = Carry;
endmodule

module PCM1BD (
  input  Clock,
  input  Enable,
  input  Place,
  input  Data,
  input  Clear,
  output Q
);

  wire and_1_out, and_2_out, d_ff_1_qn, not_1_out, or_1_out;

  and and_1 (and_1_out, Place, Data);
  and and_2 (and_2_out, Place, not_1_out);
  not not_1 (not_1_out, Data);
  D_Flip_Flop #(.trigger("falling")) d_ff_1 (
    .clk(Clock), .D(d_ff_1_qn), .Q(Q), .Qn(d_ff_1_qn), .preset(and_1_out), .en(Enable), .reset(or_1_out));
  or or_1 (or_1_out, and_2_out, Clear);

  // Notes on the sheet:
  //   D0
endmodule

module CMP4D2 (
  input  Clock,
  input  Count,
  input  Clear,
  input  Choice,
  input  [3:0] Data,
  output [3:0] Output,
  output Carry
);

  wire and_1_out, not_1_out, not_2_out, not_3_out;

  not not_1 (not_1_out, Clear);
  and and_1 (and_1_out, Clock, not_1_out, Choice, not_2_out);
  not not_2 (not_2_out, Count);
  not not_3 (not_3_out, Clock);
  PCM1BD pcm1bd_1 (.Clock(not_3_out), .Enable(Count), .Place(and_1_out), .Data(Data[0]), .Clear(Clear), .Q(Output[0]));
  PCM1BD pcm1bd_2 (.Clock(Output[0]), .Enable(Count), .Place(and_1_out), .Data(Data[1]), .Clear(Clear), .Q(Output[1]));
  PCM1BD pcm1bd_3 (.Clock(Output[1]), .Enable(Count), .Place(and_1_out), .Data(Data[2]), .Clear(Clear), .Q(Output[2]));
  PCM1BD pcm1bd_4 (.Clock(Output[2]), .Enable(Count), .Place(and_1_out), .Data(Data[3]), .Clear(Clear), .Q(Carry));

  assign Output[3] = Carry;
endmodule

module PDM1BD (
  input  Clock,
  input  Enable,
  input  Place,
  input  Data,
  input  Clear,
  output Q
);

  wire and_1_out, and_2_out, d_ff_1_qn, not_1_out, or_1_out;

  and and_1 (and_1_out, Place, Data);
  and and_2 (and_2_out, Place, not_1_out);
  not not_1 (not_1_out, Data);
  D_Flip_Flop d_ff_1 (
    .clk(Clock), .D(d_ff_1_qn), .Q(Q), .Qn(d_ff_1_qn), .preset(and_1_out), .en(Enable), .reset(or_1_out));
  or or_1 (or_1_out, and_2_out, Clear);

  // Notes on the sheet:
  //   D0
endmodule

module DMP4D2 (
  input  Clock,
  input  Count,
  input  Clear,
  input  Choice,
  input  [3:0] in_5,
  output [3:0] Output,
  output Carry
);

  wire and_1_out, not_1_out, not_2_out;

  not not_1 (not_1_out, Clear);
  and and_1 (and_1_out, Clock, not_1_out, Choice, not_2_out);
  not not_2 (not_2_out, Count);
  PDM1BD pdm1bd_1 (.Clock(Clock), .Enable(Count), .Place(and_1_out), .Data(in_5[0]), .Clear(Clear), .Q(Output[0]));
  PDM1BD pdm1bd_2 (.Clock(Output[0]), .Enable(Count), .Place(and_1_out), .Data(in_5[1]), .Clear(Clear), .Q(Output[1]));
  PDM1BD pdm1bd_3 (.Clock(Output[1]), .Enable(Count), .Place(and_1_out), .Data(in_5[2]), .Clear(Clear), .Q(Output[2]));
  PDM1BD pdm1bd_4 (.Clock(Output[2]), .Enable(Count), .Place(and_1_out), .Data(in_5[3]), .Clear(Clear), .Q(Carry));

  assign Output[3] = Carry;
endmodule

module MCMP4 (
  input  Clock,
  input  Count,
  input  Clear,
  input  Choice,
  input  [3:0] Data,
  output [3:0] Output,
  output Carry
);

  wire and_1_out, and_4_out, and_6_out, and_8_out, d_ff_1_qn, d_ff_2_qn, d_ff_3_qn, d_ff_4_qn, d_ff_5_qn,
       d_ff_6_qn, d_ff_7_qn, d_ff_8_qn, not_1_out, not_2_out, not_3_out, not_5_out, not_6_out, or_1_out,
       or_2_out, or_3_out, or_4_out;
  wire [3:0] and_2_out, and_3_out, and_5_out, and_7_out, bit_extender_1_out, bit_extender_2_out,
       bit_extender_3_out, d_ff_1_q, d_ff_2_q, not_4_out;

  not not_1 (not_1_out, and_1_out);
  not not_2 (not_2_out, Clear);
  and and_1 (and_1_out, Clock, not_2_out, Choice, not_3_out);
  not not_3 (not_3_out, Count);
  assign bit_extender_1_out = {{3{and_1_out}}, and_1_out};  // Bit_Extender bit_extender_1
  assign and_2_out = bit_extender_1_out & Data;  // AND_Gate and_2, 4 bits wide
  assign and_3_out = bit_extender_1_out & not_4_out;  // AND_Gate and_3, 4 bits wide
  assign not_4_out = ~Data;  // NOT_Gate not_4, 4 bits wide
  and and_4 (and_4_out, Clear, not_1_out);
  or or_1 (or_1_out, and_4_out, and_3_out[0]);
  or or_2 (or_2_out, and_4_out, and_3_out[1]);
  or or_3 (or_3_out, and_4_out, and_3_out[2]);
  or or_4 (or_4_out, and_4_out, and_3_out[3]);
  not not_5 (not_5_out, Clock);
  D_Flip_Flop #(.trigger("falling")) d_ff_1 (
    .clk(not_5_out), .D(d_ff_1_qn), .Q(d_ff_1_q[0]), .Qn(d_ff_1_qn), .preset(and_2_out[0]), .en(Count),
    .reset(or_1_out));
  D_Flip_Flop d_ff_2 (
    .clk(Clock), .D(d_ff_2_qn), .Q(d_ff_2_q[0]), .Qn(d_ff_2_qn), .preset(and_2_out[0]), .en(Count),
    .reset(or_1_out));
  D_Flip_Flop #(.trigger("falling")) d_ff_3 (
    .clk(d_ff_1_q[0]), .D(d_ff_3_qn), .Q(d_ff_1_q[1]), .Qn(d_ff_3_qn), .preset(and_2_out[1]), .en(Count),
    .reset(or_2_out));
  D_Flip_Flop d_ff_4 (
    .clk(d_ff_2_q[0]), .D(d_ff_4_qn), .Q(d_ff_2_q[1]), .Qn(d_ff_4_qn), .preset(and_2_out[1]), .en(Count),
    .reset(or_2_out));
  D_Flip_Flop #(.trigger("falling")) d_ff_5 (
    .clk(d_ff_1_q[1]), .D(d_ff_5_qn), .Q(d_ff_1_q[2]), .Qn(d_ff_5_qn), .preset(and_2_out[2]), .en(Count),
    .reset(or_3_out));
  D_Flip_Flop d_ff_6 (
    .clk(d_ff_2_q[1]), .D(d_ff_6_qn), .Q(d_ff_2_q[2]), .Qn(d_ff_6_qn), .preset(and_2_out[2]), .en(Count),
    .reset(or_3_out));
  D_Flip_Flop #(.trigger("falling")) d_ff_7 (
    .clk(d_ff_1_q[2]), .D(d_ff_7_qn), .Q(d_ff_1_q[3]), .Qn(d_ff_7_qn), .preset(and_2_out[3]), .en(Count),
    .reset(or_4_out));
  D_Flip_Flop d_ff_8 (
    .clk(d_ff_2_q[2]), .D(d_ff_8_qn), .Q(d_ff_2_q[3]), .Qn(d_ff_8_qn), .preset(and_2_out[3]), .en(Count),
    .reset(or_4_out));
  assign bit_extender_2_out = {{3{not_6_out}}, not_6_out};  // Bit_Extender bit_extender_2
  not not_6 (not_6_out, Choice);
  assign bit_extender_3_out = {{3{Choice}}, Choice};  // Bit_Extender bit_extender_3
  assign and_5_out = d_ff_1_q & bit_extender_2_out;  // AND_Gate and_5, 4 bits wide
  assign Output = and_5_out | and_7_out;  // OR_Gate or_5, 4 bits wide
  and and_6 (and_6_out, d_ff_1_q[3], not_6_out);
  assign and_7_out = d_ff_2_q & bit_extender_3_out;  // AND_Gate and_7, 4 bits wide
  and and_8 (and_8_out, d_ff_2_q[3], Choice);
  or or_6 (Carry, and_6_out, and_8_out);

  // Notes on the sheet:
  //   Q0
  //   D1
  //   D0
  //   Q0
  //   D0
  //   Q1
  //   D2
  //   Q1
  //   D1
  //   D2
  //   Q2
  //   D3
  //   Q2
  //   D3
  //   Q3
  //   Q3
endmodule

module PDC1BD (
  input  Clock,
  input  Enable,
  input  Place,
  input  Data,
  input  Clear,
  input  Countdown,
  output Q
);

  wire and_1_out, and_2_out, and_3_out, and_4_out, d_ff_1_q, d_ff_1_qn, d_ff_2_q, d_ff_2_qn, not_1_out,
       not_2_out, or_1_out;

  and and_1 (and_1_out, Place, Data);
  and and_2 (and_2_out, Place, not_1_out);
  not not_1 (not_1_out, Data);
  or or_1 (or_1_out, and_2_out, Clear);
  D_Flip_Flop #(.trigger("falling")) d_ff_1 (
    .clk(Clock), .D(d_ff_1_qn), .Q(d_ff_1_q), .Qn(d_ff_1_qn), .preset(and_1_out), .en(Enable),
    .reset(or_1_out));
  D_Flip_Flop d_ff_2 (
    .clk(Clock), .D(d_ff_2_qn), .Q(d_ff_2_q), .Qn(d_ff_2_qn), .preset(and_1_out), .en(Enable),
    .reset(or_1_out));
  and and_3 (and_3_out, d_ff_1_q, not_2_out);
  not not_2 (not_2_out, Countdown);
  and and_4 (and_4_out, d_ff_2_q, Countdown);
  or or_2 (Q, and_3_out, and_4_out);
endmodule

module DCP4D2 (
  input  Clock,
  input  Count,
  input  Clear,
  input  Choice,
  input  [3:0] Data,
  output [3:0] Output,
  output Carry
);

  wire and_1_out, and_2_out, nor_1_out, not_1_out, not_2_out, or_1_out;

  and and_1 (and_1_out, Clock, Choice);
  or or_1 (or_1_out, and_1_out, nor_1_out);
  nor nor_1 (nor_1_out, Clock, Choice);
  not not_1 (not_1_out, Clear);
  not not_2 (not_2_out, Count);
  PDC1BD pdc1bd_1 (
    .Clock(or_1_out), .Enable(Count), .Place(and_2_out), .Data(Data[0]), .Clear(Clear), .Countdown(Choice),
    .Q(Output[0]));
  and and_2 (and_2_out, Clock, not_1_out, Choice, not_2_out);
  PDC1BD pdc1bd_2 (
    .Clock(Output[0]), .Enable(Count), .Place(and_2_out), .Data(Data[1]), .Clear(Clear), .Countdown(Choice),
    .Q(Output[1]));
  PDC1BD pdc1bd_3 (
    .Clock(Output[1]), .Enable(Count), .Place(and_2_out), .Data(Data[2]), .Clear(Clear), .Countdown(Choice),
    .Q(Output[2]));
  PDC1BD pdc1bd_4 (
    .Clock(Output[2]), .Enable(Count), .Place(and_2_out), .Data(Data[3]), .Clear(Clear), .Countdown(Choice),
    .Q(Carry));

  assign Output[3] = Carry;
endmodule

module DCP4D3 (
  input  Clock,
  input  Count,
  input  Clear,
  input  Choice,
  input  [3:0] Data,
  output [3:0] Output,
  output Carry
);

  wire c4o_1_clock_2, c4o_1_place;

  C4O c4o_1 (
    .Clock(Clock), .Clear(Clear), .Choice(Choice), .Count(Count), .Clock_2(c4o_1_clock_2), .Place(c4o_1_place));
  PDC1BD pdc1bd_1 (
    .Clock(c4o_1_clock_2), .Enable(Count), .Place(c4o_1_place), .Data(Data[0]), .Clear(Clear),
    .Countdown(Choice), .Q(Output[0]));
  PDC1BD pdc1bd_2 (
    .Clock(Output[0]), .Enable(Count), .Place(c4o_1_place), .Data(Data[1]), .Clear(Clear),
    .Countdown(Choice), .Q(Output[1]));
  PDC1BD pdc1bd_3 (
    .Clock(Output[1]), .Enable(Count), .Place(c4o_1_place), .Data(Data[2]), .Clear(Clear),
    .Countdown(Choice), .Q(Output[2]));
  PDC1BD pdc1bd_4 (
    .Clock(Output[2]), .Enable(Count), .Place(c4o_1_place), .Data(Data[3]), .Clear(Clear),
    .Countdown(Choice), .Q(Carry));

  assign Output[3] = Carry;
endmodule

module PDC4BD (
  input  Clock,
  input  Place,
  input  Enable,
  input  Countdown,
  input  Clear,
  input  [3:0] Data,
  output [3:0] Output,
  output Carry
);

  PDC1BD pdc1bd_1 (
    .Clock(Clock), .Enable(Enable), .Place(Place), .Data(Data[0]), .Clear(Clear), .Countdown(Countdown),
    .Q(Output[0]));
  PDC1BD pdc1bd_2 (
    .Clock(Output[0]), .Enable(Enable), .Place(Place), .Data(Data[1]), .Clear(Clear), .Countdown(Countdown),
    .Q(Output[1]));
  PDC1BD pdc1bd_3 (
    .Clock(Output[1]), .Enable(Enable), .Place(Place), .Data(Data[2]), .Clear(Clear), .Countdown(Countdown),
    .Q(Output[2]));
  PDC1BD pdc1bd_4 (
    .Clock(Output[2]), .Enable(Enable), .Place(Place), .Data(Data[3]), .Clear(Clear), .Countdown(Countdown),
    .Q(Carry));

  assign Output[3] = Carry;
endmodule

module DCP4D4 (
  input  Clock,
  input  Count,
  input  Clear,
  input  Choice,
  input  [3:0] Data,
  output [3:0] Output,
  output Carry
);

  wire c4o_1_clock_2, c4o_1_place;

  C4O c4o_1 (
    .Clock(Clock), .Clear(Clear), .Choice(Choice), .Count(Count), .Clock_2(c4o_1_clock_2), .Place(c4o_1_place));
  PDC4BD pdc4bd_1 (
    .Clock(c4o_1_clock_2), .Place(c4o_1_place), .Enable(Count), .Countdown(Choice), .Clear(Clear),
    .Data(Data), .Output(Output), .Carry(Carry));
endmodule

module DCP8D3 (
  input  Clock,
  input  Count,
  input  Clear,
  input  Choice,
  input  [7:0] Data,
  output [7:0] Output,
  output Carry
);

  wire c4o_1_clock_2, c4o_1_place;

  C4O c4o_1 (
    .Clock(Clock), .Clear(Clear), .Choice(Choice), .Count(Count), .Clock_2(c4o_1_clock_2), .Place(c4o_1_place));
  PDC1BD pdc1bd_1 (
    .Clock(c4o_1_clock_2), .Enable(Count), .Place(c4o_1_place), .Data(Data[0]), .Clear(Clear),
    .Countdown(Choice), .Q(Output[0]));
  PDC1BD pdc1bd_2 (
    .Clock(Output[0]), .Enable(Count), .Place(c4o_1_place), .Data(Data[1]), .Clear(Clear),
    .Countdown(Choice), .Q(Output[1]));
  PDC1BD pdc1bd_3 (
    .Clock(Output[1]), .Enable(Count), .Place(c4o_1_place), .Data(Data[2]), .Clear(Clear),
    .Countdown(Choice), .Q(Output[2]));
  PDC1BD pdc1bd_4 (
    .Clock(Output[2]), .Enable(Count), .Place(c4o_1_place), .Data(Data[3]), .Clear(Clear),
    .Countdown(Choice), .Q(Output[3]));
  PDC1BD pdc1bd_5 (
    .Clock(Output[3]), .Enable(Count), .Place(c4o_1_place), .Data(Data[4]), .Clear(Clear),
    .Countdown(Choice), .Q(Output[4]));
  PDC1BD pdc1bd_6 (
    .Clock(Output[4]), .Enable(Count), .Place(c4o_1_place), .Data(Data[5]), .Clear(Clear),
    .Countdown(Choice), .Q(Output[5]));
  PDC1BD pdc1bd_7 (
    .Clock(Output[6]), .Enable(Count), .Place(c4o_1_place), .Data(Data[7]), .Clear(Clear),
    .Countdown(Choice), .Q(Carry));
  PDC1BD pdc1bd_8 (
    .Clock(Output[5]), .Enable(Count), .Place(c4o_1_place), .Data(Data[6]), .Clear(Clear),
    .Countdown(Choice), .Q(Output[6]));

  assign Output[7] = Carry;
endmodule

module DCP8D4 (
  input  Clock,
  input  Count,
  input  Clear,
  input  Choice,
  input  [7:0] Data,
  output [7:0] Output,
  output Carry
);

  wire c4o_1_clock_2, c4o_1_place, pdc4bd_1_carry;

  C4O c4o_1 (
    .Clock(Clock), .Clear(Clear), .Choice(Choice), .Count(Count), .Clock_2(c4o_1_clock_2), .Place(c4o_1_place));
  PDC4BD pdc4bd_1 (
    .Clock(c4o_1_clock_2), .Place(c4o_1_place), .Enable(Count), .Countdown(Choice), .Clear(Clear),
    .Data(Data[3:0]), .Output(Output[3:0]), .Carry(pdc4bd_1_carry));
  PDC4BD pdc4bd_2 (
    .Clock(pdc4bd_1_carry), .Place(c4o_1_place), .Enable(Count), .Countdown(Choice), .Clear(Clear),
    .Data(Data[7:4]), .Output(Output[7:4]), .Carry(Carry));
endmodule

module PDC8BD (
  input  Clock,
  input  Place,
  input  Enable,
  input  Countdown,
  input  Clear,
  input  [7:0] Data,
  output [7:0] Output,
  output Carry
);

  wire pdc4bd_1_carry;

  PDC4BD pdc4bd_1 (
    .Clock(Clock), .Place(Place), .Enable(Enable), .Countdown(Countdown), .Clear(Clear), .Data(Data[3:0]),
    .Output(Output[3:0]), .Carry(pdc4bd_1_carry));
  PDC4BD pdc4bd_2 (
    .Clock(pdc4bd_1_carry), .Place(Place), .Enable(Enable), .Countdown(Countdown), .Clear(Clear),
    .Data(Data[7:4]), .Output(Output[7:4]), .Carry(Carry));
endmodule

module DCP8D5 (
  input  Clock,
  input  Count,
  input  Clear,
  input  Choice,
  input  [7:0] Data,
  output [7:0] Output,
  output Carry
);

  wire c4o_1_clock_2, c4o_1_place;

  C4O c4o_1 (
    .Clock(Clock), .Clear(Clear), .Choice(Choice), .Count(Count), .Clock_2(c4o_1_clock_2), .Place(c4o_1_place));
  PDC8BD pdc8bd_1 (
    .Clock(c4o_1_clock_2), .Place(c4o_1_place), .Enable(Count), .Countdown(Choice), .Clear(Clear),
    .Data(Data), .Output(Output), .Carry(Carry));
endmodule

module C4O (
  input  Clock,
  input  Clear,
  input  Choice,
  input  Count,
  output Clock_2,
  output Place
);

  wire and_1_out, nor_1_out, not_1_out, not_2_out;

  and and_1 (and_1_out, Clock, Choice);
  or or_1 (Clock_2, and_1_out, nor_1_out);
  nor nor_1 (nor_1_out, Clock, Choice);
  not not_1 (not_1_out, Clear);
  and and_2 (Place, Clock, not_1_out, Choice, not_2_out);
  not not_2 (not_2_out, Count);
endmodule
