// Logisim project 11_RAND_V.circ as structural Verilog: 8 circuits, main circuit main
module main (
  input  H,
  input  Enable,
  input  [7:0] MAX,
  input  [7:0] MIN
);

  wire random_2_p5, random_3_p4;
  wire [3:0] random_1_out, sram4m_1_output, srand4_1_output, srand4s_1_output;
  wire [7:0] randm_1_output, srand8_1_output, sranmm_1_o;

  // Probe on MAX
  // Probe on MAX
  // Probe on MAX
  // Probe on MIN
  // Probe on MIN
  // Probe on MIN
  Random #(.width(4)) random_1 (.clk(H), .next(Enable), .out(random_1_out), .clr(1'b0));
  SRAND4 srand4_1 (.Clear(1'b0), .Enable(Enable), .Clock(H), .Output(srand4_1_output));  // open: Clock_out
  SRAND8 srand8_1 (.Clear(1'b0), .Enable(Enable), .Clock(H), .Output(srand8_1_output));  // open: Clock_out
  RANDM randm_1 (.H(H), .Enable(Enable), .Max(MAX), .Output(randm_1_output));  // open: def
  SRANMM sranmm_1 (.Max(MAX), .Min(MIN), .H(H), .Enable(Enable), .O(sranmm_1_o));
  // Probe on random_1_out
  // Probe on random_1_out
  // Probe on random_1_out
  // Probe on random_1_out
  // Probe on srand4_1_output
  // Probe on srand4_1_output
  // Probe on srand4_1_output
  // Probe on srand4_1_output
  // Probe on srand8_1_output
  // Probe on srand8_1_output
  // Probe on srand8_1_output
  // Probe on srand8_1_output
  // Probe on randm_1_output
  // Probe on randm_1_output
  // Probe on randm_1_output
  // Probe on randm_1_output
  // Probe on sranmm_1_o
  // Probe on sranmm_1_o
  // Probe on sranmm_1_o
  // Probe on sranmm_1_o
  SRAM4M sram4m_1 (.Clear(1'b0), .Enable(Enable), .Clock(H), .Output(sram4m_1_output));  // open: Clock_out
  SRAND4S srand4s_1 (.Clear(1'b0), .Enable(Enable), .Clock(H), .Output(srand4s_1_output));  // open: Clock_out
  // Random random_2: pin names not known; wires that end beside it: H, Enable, MAX, MIN, random_2_p5
  // Probe on sram4m_1_output
  // Probe on sram4m_1_output
  // Probe on sram4m_1_output
  // Probe on sram4m_1_output
  // Probe on srand4s_1_output
  // Probe on srand4s_1_output
  // Probe on srand4s_1_output
  // Probe on srand4s_1_output
  // Random random_3: pin names not known; wires that end beside it: H, Enable, MAX, random_3_p4
  // Probe on random_3_p4
  // Probe on random_3_p4
  // Probe on random_3_p4
  // Probe on random_3_p4
  // Probe on random_2_p5
  // Probe on random_2_p5
  // Probe on random_2_p5
  // Probe on random_2_p5

  // Notes on the sheet:
  //   RANDM
  //   other_chip8.circ
  //   Other.jar
  //   Other.jar
endmodule

module SRAND4 (
  input  Clear,
  input  Enable,
  input  Clock,
  output Clock_out,
  output [3:0] Output
);

  wire and_1_out, not_1_out, not_2_out, not_3_out, not_4_out, or_1_out, xor_1_out;

  or or_1 (or_1_out, xor_1_out, and_1_out);
  and and_1 (and_1_out, not_1_out, not_2_out, not_3_out, not_4_out);
  D_Flip_Flop d_ff_1 (.clk(Clock), .D(or_1_out), .Q(Output[0]), .preset(1'b0), .en(Enable), .reset(Clear));  // open: Qn
  not not_1 (not_1_out, Output[3]);
  not not_2 (not_2_out, Output[2]);
  not not_3 (not_3_out, Output[1]);
  not not_4 (not_4_out, Output[0]);
  xor xor_1 (xor_1_out, Clock_out, Output[1]);
  D_Flip_Flop d_ff_2 (
    .clk(Clock), .D(Output[0]), .Q(Output[1]), .preset(1'b0), .en(Enable), .reset(Clear));  // open: Qn
  D_Flip_Flop d_ff_3 (
    .clk(Clock), .D(Output[1]), .Q(Output[2]), .preset(1'b0), .en(Enable), .reset(Clear));  // open: Qn
  D_Flip_Flop d_ff_4 (
    .clk(Clock), .D(Output[2]), .Q(Output[3]), .preset(1'b0), .en(Enable), .reset(Clear));  // open: Qn
  D_Flip_Flop d_ff_5 (
    .clk(Clock), .D(Output[3]), .Q(Clock_out), .preset(1'b0), .en(Enable), .reset(Clear));  // open: Qn
  // Probe on Output
  // Probe on Output

  // Notes on the sheet:
  //   E0
  //   Q0
  //   Q1
  //   Q1
  //   Q2
  //   Q3
  //   Q4
endmodule

module SRAM4M (
  input  Clear,
  input  Enable,
  input  Clock,
  output Clock_out,
  output [3:0] Output
);

  wire nor_1_out, or_1_out, xor_1_out;

  or or_1 (or_1_out, xor_1_out, nor_1_out);
  nor nor_1 (nor_1_out, Output[3], Output[2], Output[1], Output[0]);
  D_Flip_Flop d_ff_1 (.clk(Clock), .D(or_1_out), .Q(Output[0]), .preset(1'b0), .en(Enable), .reset(Clear));  // open: Qn
  xor xor_1 (xor_1_out, Clock_out, Output[1]);
  D_Flip_Flop d_ff_2 (
    .clk(Clock), .D(Output[0]), .Q(Output[1]), .preset(1'b0), .en(Enable), .reset(Clear));  // open: Qn
  D_Flip_Flop d_ff_3 (
    .clk(Clock), .D(Output[1]), .Q(Output[2]), .preset(1'b0), .en(Enable), .reset(Clear));  // open: Qn
  D_Flip_Flop d_ff_4 (
    .clk(Clock), .D(Output[2]), .Q(Output[3]), .preset(1'b0), .en(Enable), .reset(Clear));  // open: Qn
  D_Flip_Flop d_ff_5 (
    .clk(Clock), .D(Output[3]), .Q(Clock_out), .preset(1'b0), .en(Enable), .reset(Clear));  // open: Qn
  // Probe on Output
  // Probe on Output

  // Notes on the sheet:
  //   E0
  //   Q0
  //   Q1
  //   Q1
  //   Q2
  //   Q3
  //   Q4
endmodule

module SRAND4S (
  input  Clear,
  input  Enable,
  input  Clock,
  output Clock_out,
  output [3:0] Output
);

  wire valinrand_1_out;

  D_Flip_Flop d_ff_1 (
    .clk(Clock), .D(valinrand_1_out), .Q(Output[0]), .preset(1'b0), .en(Enable), .reset(Clear));  // open: Qn
  D_Flip_Flop d_ff_2 (
    .clk(Clock), .D(Output[0]), .Q(Output[1]), .preset(1'b0), .en(Enable), .reset(Clear));  // open: Qn
  D_Flip_Flop d_ff_3 (
    .clk(Clock), .D(Output[1]), .Q(Output[2]), .preset(1'b0), .en(Enable), .reset(Clear));  // open: Qn
  D_Flip_Flop d_ff_4 (
    .clk(Clock), .D(Output[2]), .Q(Output[3]), .preset(1'b0), .en(Enable), .reset(Clear));  // open: Qn
  VALINRAND valinrand_1 (
    .IN0(Output[0]), .IN1(Output[1]), .IN2(Output[2]), .IN3(Output[3]), .IN4(Clock_out), .Out(valinrand_1_out));
  D_Flip_Flop d_ff_5 (
    .clk(Clock), .D(Output[3]), .Q(Clock_out), .preset(1'b0), .en(Enable), .reset(Clear));  // open: Qn
  // Probe on Output
  // Probe on Output

  // Notes on the sheet:
  //   E0
  //   Q0
  //   Q1
  //   Q2
  //   Q3
  //   Q4
endmodule

module SRAND8 (
  input  Clock,
  input  Enable,
  input  Clear,
  output [7:0] Output,
  output Clock_out
);

  wire srand4_1_clock_out;

  SRAND4 srand4_1 (.Clear(Clear), .Enable(Enable), .Clock(Clock), .Clock_out(srand4_1_clock_out), .Output(Output[3:0]));
  SRAND4 srand4_2 (
    .Clear(Clear), .Enable(Enable), .Clock(srand4_1_clock_out), .Clock_out(Clock_out), .Output(Output[7:4]));
  // Probe on Output
  // Probe on Output
endmodule

module SRANMM (
  input  [7:0] Max,
  input  [7:0] Min,
  input  H,
  input  Enable,
  output [7:0] O
);

  wire [7:0] bit_extender_3_out, randm_1_output;
  wire [8:0] adder_1_out, bit_extender_1_out, bit_extender_2_out, bit_extender_4_out, subtractor_1_out;

  assign bit_extender_1_out = {{1{1'b0}}, Max};  // Bit_Extender bit_extender_1
  assign bit_extender_2_out = {{1{1'b0}}, Min};  // Bit_Extender bit_extender_2
  Subtractor #(.width(9)) subtractor_1 (
    .a(bit_extender_1_out), .b(bit_extender_2_out), .out(subtractor_1_out), .bin(1'b0));  // open: bout
  Bit_Extender #(.in_width(9), .out_width(8)) bit_extender_3 (.in(subtractor_1_out), .out(bit_extender_3_out));
  RANDM randm_1 (.H(H), .Enable(Enable), .Max(bit_extender_3_out), .Output(randm_1_output));  // open: def
  assign bit_extender_4_out = {{1{1'b0}}, randm_1_output};  // Bit_Extender bit_extender_4
  Adder #(.width(9)) adder_1 (
    .a(bit_extender_4_out), .b(bit_extender_2_out), .out(adder_1_out), .cin(1'b0));  // open: cout
  Bit_Extender #(.in_width(9), .out_width(8)) bit_extender_5 (.in(adder_1_out), .out(O));

  // Notes on the sheet:
  //   RANDM
  //   other_chip8.circ
endmodule

module VALINRAND (
  input  IN0,
  input  IN1,
  input  IN2,
  input  IN3,
  input  IN4,
  output Out
);

  wire nor_1_out, xor_1_out;

  xor xor_1 (xor_1_out, IN1, IN4);
  nor nor_1 (nor_1_out, IN0, IN1, IN2, IN3);
  or or_1 (Out, nor_1_out, xor_1_out);

  // Notes on the sheet:
  //   O0
  //   O1
endmodule

module SUITE (
  input  Clear,
  input  Enable,
  input  Clock,
  output Clock_out,
  output [3:0] Output
);

  D_Flip_Flop d_ff_1 (.clk(Clock), .D(1'b1), .Q(Output[0]), .preset(1'b0), .en(Enable), .reset(Clear));  // open: Qn
  D_Flip_Flop d_ff_2 (
    .clk(Clock), .D(Output[0]), .Q(Output[1]), .preset(1'b0), .en(Enable), .reset(Clear));  // open: Qn
  D_Flip_Flop d_ff_3 (
    .clk(Clock), .D(Output[1]), .Q(Output[2]), .preset(1'b0), .en(Enable), .reset(Clear));  // open: Qn
  D_Flip_Flop d_ff_4 (
    .clk(Clock), .D(Output[2]), .Q(Output[3]), .preset(1'b0), .en(Enable), .reset(Clear));  // open: Qn
  D_Flip_Flop d_ff_5 (
    .clk(Clock), .D(Output[3]), .Q(Clock_out), .preset(1'b0), .en(Enable), .reset(Clear));  // open: Qn
  // Probe on Output
  // Probe on Output

  // Notes on the sheet:
  //   E0
endmodule
