// Logisim project themult.circ as structural Verilog: 4 circuits, main circuit main
module main (
  input  in_1,
  input  [1:0] in_2,
  input  in_3,
  input  [1:0] in_4,
  input  in_5,
  input  [1:0] in_6,
  input  [3:0] in_7,
  input  [3:0] in_8,
  input  [3:0] in_9,
  output out_10,
  output out_11,
  output [1:0] out_12,
  output [1:0] out_13,
  output out_14,
  output out_15,
  output [1:0] out_16,
  output [1:0] out_17,
  output [3:0] out_18,
  output [3:0] out_19,
  output [3:0] out_20,
  output [3:0] out_21
);

  Multiplier #(.width(1)) multiplier_1 (.a(in_3), .b(in_5), .out(out_10), .cin(in_1), .cout(out_11));
  Multiplier #(.width(2)) multiplier_2 (.a(in_4), .b(in_6), .out(out_12), .cin(in_2), .cout(out_13));
  Multiplier #(.width(4)) multiplier_3 (.a(in_8), .b(in_9), .out(out_18), .cin(in_7), .cout(out_19));
  MUL1B mul1b_1 (.R(in_1), .A(in_3), .B(in_5), .S(out_14), .RS(out_15));
  MUL2B mul2b_1 (.in_1(in_2), .in_2(in_4), .in_3(in_6), .out_4(out_16), .out_5(out_17));
  MUL4B mul4b_1 (.in_1(in_7), .out_4(out_20), .in_2(in_8), .out_5(out_21), .in_3(in_9));

  // Other names for the same wires on the sheet: A = in_3; A2b[1:0] = in_4; A4b[3:0] = in_8; B = in_5;
  //   B2b[1:0] = in_6; B4b[3:0] = in_9; R = in_1; R2b[1:0] = in_2; R4b[3:0] = in_7; RS1 = out_11; RS2 = out_15;
  //   RS2b1[1:0] = out_13; RS2b2[1:0] = out_17; RS4b1[3:0] = out_19; RS4b2[3:0] = out_21; S1 = out_10; S2 = out_14;
  //   S2b1[1:0] = out_12; S2b2[1:0] = out_16; S4b1[3:0] = out_18; S4b2[3:0] = out_20
endmodule

module MUL1B (
  input  R,
  input  A,
  input  B,
  output S,
  output RS
);

  wire and_1_out, and_2_out, and_3_out, not_1_out, not_2_out;

  and and_1 (and_1_out, A, B);
  not not_1 (not_1_out, R);
  not not_2 (not_2_out, and_1_out);
  and and_2 (and_2_out, not_1_out, and_1_out);
  or or_1 (S, and_2_out, and_3_out);
  and and_3 (and_3_out, not_2_out, R);
  and and_4 (RS, and_1_out, R);
endmodule

module MUL2B (
  input  [1:0] in_1,
  input  [1:0] in_2,
  input  [1:0] in_3,
  output [1:0] out_4,
  output [1:0] out_5
);

  wire [1:0] adder_1_out, mul1b_1_s;
  wire [2:0] bit_extender_1_out;
  wire [2:1] mul1b_3_s;

  MUL1B mul1b_1 (.R(1'b0), .A(in_2[0]), .B(in_3[0]), .S(mul1b_1_s[0]));  // open: RS
  MUL1B mul1b_2 (.R(1'b0), .A(in_2[1]), .B(in_3[0]), .S(mul1b_1_s[1]));  // open: RS
  MUL1B mul1b_3 (.R(1'b0), .A(in_2[0]), .B(in_3[1]), .S(mul1b_3_s[1]));  // open: RS
  MUL1B mul1b_4 (.R(1'b0), .A(in_2[1]), .B(in_3[1]), .S(mul1b_3_s[2]));  // open: RS
  Adder #(.width(2)) adder_1 (.a(in_1), .b(mul1b_1_s), .out(adder_1_out), .cin(1'b0));  // open: cout
  assign bit_extender_1_out = {{1{1'b0}}, adder_1_out};  // Bit_Extender bit_extender_1
  Adder #(.width(3)) adder_2 (
    .a(bit_extender_1_out), .b({mul1b_3_s, 1'b0}), .out({out_5[0], out_4}), .cin(1'b0), .cout(out_5[1]));

  // Other names for the same wires on the sheet: A1 = in_2[0]; A2 = in_2[1]; B1 = in_3[0]; B2 = in_3[1];
  //   R1[1:0] = in_1
endmodule

module MUL4B (
  input  [3:0] in_1,
  input  [3:0] in_2,
  input  [3:0] in_3,
  output [3:0] out_4,
  output [3:0] out_5
);

  MUL2B mul2b_1 (.in_1(in_1[1:0]), .in_2(in_2[1:0]), .in_3(in_3[1:0]), .out_4(out_4[1:0]), .out_5(out_5[1:0]));
  MUL2B mul2b_2 (.in_1(in_1[3:2]), .in_2(in_2[3:2]), .in_3(in_3[3:2]), .out_4(out_4[3:2]), .out_5(out_5[3:2]));

  // Other names for the same wires on the sheet: R1[1:0] = in_1[1:0]; R2[1:0] = in_1[3:2]; A1[1:0] = in_2[1:0];
  //   A2[1:0] = in_2[3:2]; B1[1:0] = in_3[1:0]; B2[1:0] = in_3[3:2]; S1[1:0] = out_4[1:0]; S2[1:0] = out_4[3:2];
  //   RS1[1:0] = out_5[1:0]; RS2[1:0] = out_5[3:2]
endmodule
